// Logisim project 4bit.circ as structural Verilog
module RS_Latch (
  input  Reset,
  input  Set,
  output Output,
  output Negated_Output
);

  nor nor_1 (Output, Reset, Negated_Output);
  nor nor_2 (Negated_Output, Output, Set);
endmodule

module D_Latch (
  input  Clock,
  input  Data,
  output Output,
  output out_4
);

  wire and_1_out, and_2_out, not_1_out;

  not not_1 (not_1_out, Data);
  and and_1 (and_1_out, Clock, not_1_out);
  and and_2 (and_2_out, Clock, Data);
  RS_Latch rs_latch_1 (.Negated_Output(out_4), .Output(Output), .Set(and_2_out), .Reset(and_1_out));

  // Notes on the sheet:
  //   Negated Output
endmodule

module D_Flip_Flop (
  input  Data,
  input  Clock,
  input  Write_Enable,
  output Output,
  output out_5
);

  wire d_latch_1_output, multiplexer_1_out, not_1_out;

  Multiplexer #(.enable("false")) multiplexer_1 (.in0(Output), .in1(Data), .out(multiplexer_1_out), .sel(Write_Enable));
  not not_1 (not_1_out, Clock);
  D_Latch d_latch_1 (.Output(d_latch_1_output), .Data(multiplexer_1_out), .Clock(Clock));  // open: out_4
  D_Latch d_latch_2 (.out_4(out_5), .Output(Output), .Data(d_latch_1_output), .Clock(not_1_out));

  // Notes on the sheet:
  //   Negated Output
endmodule
