// Logisim project Pipeline.circ as structural Verilog
module CPU (
  input  RAM_CLEAR,
  input  PC_RESET
);

  wire CLK_out, fwd_stall_unit_1_bubble, fwd_stall_unit_1_if_id_write, fwd_stall_unit_1_pc_write,
       jr_handle_1_jr, main_ctrl_1_alusrc, main_ctrl_1_extop, main_ctrl_1_link, main_ctrl_1_memread,
       main_ctrl_1_memtoreg, main_ctrl_1_memwrite, main_ctrl_1_regwrite, next_pc_1_pc_src,
       r_type_test_1_r_type, reg_ex_1_alusrc_out, reg_ex_1_extop_out, reg_mem_1_memread_out,
       reg_mem_1_memtoreg_out, reg_mem_1_memwrite_out, reg_mem_2_memread_out, reg_mem_2_memtoreg_out,
       reg_mem_2_memwrite_out, reg_wb_1_regwrite_out, reg_wb_2_regwrite_out, registerfile_1_p3;
  wire [1:0] fwd_stall_unit_1_fwd_a, fwd_stall_unit_1_fwd_b;
  wire [2:0] main_ctrl_1_jb_ctrl;
  wire [3:0] alu_ctrl_1_alu_ctrl;
  wire [4:0] EX_MEM_RW_q, ID_EX_RW_q, ID_EX_SA_q, IF_ID_OP_q_2, multiplexer_2_out, multiplexer_3_out,
       registerfile_1_p4;
  wire [5:0] reg_funct_op_1_funct_out, reg_funct_op_1_opcode_out;
  wire [15:0] ID_EX_IMM_q;
  wire [29:0] IF_ID_PC_q, next_pc_1_address;
  wire [31:0] bit_extender_1_out_32b, EX_MEM_ALU_Result_q, EX_MEM_DATA_IN_q, ID_EX_A_q, ID_EX_B_q,
       IF_ID_OP_q, MEM_WB_WriteData_q, mips_alu_1_p5, mips_ram_1_p7, mipsprogramrom_1_p2, multiplexer_1_out,
       multiplexer_4_out, multiplexer_5_out, multiplexer_6_out, multiplexer_7_out, pc_1_pc,
       registerfile_1_p7, registerfile_1_p8;
  wire [31:2] pc_1_pc_incr_30b;

  Clock CLK (.out(CLK_out));
  PC pc_1 (
    .JR(jr_handle_1_jr), .REG_BUS(ID_EX_A_q), .PC_SRC(next_pc_1_pc_src), .ADDR(next_pc_1_address),
    .PC_RESET(PC_RESET), .CLK(CLK_out), .PC_Write(fwd_stall_unit_1_pc_write), .PC_INCR_30b(pc_1_pc_incr_30b),
    .PC(pc_1_pc));
  // MIPSProgramROM mipsprogramrom_1: pin names not known; wires that end beside it: pc_1_pc, mipsprogramrom_1_p2
  Register #(.width(30), .trigger("falling")) IF_ID_PC (
    .D(pc_1_pc_incr_30b), .en(1'b1), .clk(CLK_out), .Q(IF_ID_PC_q));  // open: clr
  Register #(.width(32), .trigger("falling")) IF_ID_OP (
    .D(mipsprogramrom_1_p2), .en(fwd_stall_unit_1_if_id_write), .clk(CLK_out),
    .Q({IF_ID_OP_q[31:11], IF_ID_OP_q_2, IF_ID_OP_q[5:0]}));  // open: clr
  // Probe on {IF_ID_OP_q[25:11], IF_ID_OP_q_2, IF_ID_OP_q[5:0]}
  // Probe on IF_ID_OP_q[31:26]
  // Probe on IF_ID_OP_q[25:21]
  // Probe on IF_ID_OP_q[20:16]
  // Probe on IF_ID_OP_q[15:11]
  // Probe on IF_ID_OP_q_2
  // Probe on IF_ID_OP_q[5:0]
  // Probe on {IF_ID_OP_q[15:11], IF_ID_OP_q_2, IF_ID_OP_q[5:0]}
  R_TYPE_TEST r_type_test_1 (.OPCODE(IF_ID_OP_q[31:26]), .R_TYPE(r_type_test_1_r_type));
  MAIN_CTRL main_ctrl_1 (
    .OPCODE(IF_ID_OP_q[31:26]), .Bubble(fwd_stall_unit_1_bubble), .RegWrite(main_ctrl_1_regwrite),
    .ExtOp(main_ctrl_1_extop), .MemRead(main_ctrl_1_memread), .MemWrite(main_ctrl_1_memwrite),
    .MemToReg(main_ctrl_1_memtoreg), .ALUSrc(main_ctrl_1_alusrc), .JB_CTRL(main_ctrl_1_jb_ctrl),
    .Link(main_ctrl_1_link));
  JR_HANDLE jr_handle_1 (.FUNCT(IF_ID_OP_q[5:0]), .R_TYPE(r_type_test_1_r_type), .JR(jr_handle_1_jr));
  FWD_STALL_UNIT fwd_stall_unit_1 (
    .RS_ID(IF_ID_OP_q[25:21]), .RT_ID(IF_ID_OP_q[20:16]), .RW_EX(ID_EX_RW_q), .RW_MEM(EX_MEM_RW_q),
    .MemRead_EX(reg_mem_1_memread_out), .FWD_A(fwd_stall_unit_1_fwd_a), .FWD_B(fwd_stall_unit_1_fwd_b),
    .PC_Write(fwd_stall_unit_1_pc_write), .IF_ID_Write(fwd_stall_unit_1_if_id_write),
    .Bubble(fwd_stall_unit_1_bubble));
  Multiplexer #(.width(32), .enable("false")) multiplexer_1 (
    .in0(MEM_WB_WriteData_q), .in1({pc_1_pc_incr_30b, 2'b00}), .out(multiplexer_1_out), .sel(main_ctrl_1_link));
  Multiplexer #(.width(5), .enable("false")) multiplexer_2 (
    .in0(multiplexer_3_out), .in1({5{1'b1}}), .out(multiplexer_2_out), .sel(main_ctrl_1_link));
  Multiplexer #(.width(5), .enable("false")) multiplexer_3 (
    .in0(IF_ID_OP_q[20:16]), .in1(IF_ID_OP_q[15:11]), .out(multiplexer_3_out), .sel(r_type_test_1_r_type));
  // RegisterFile registerfile_1: pin names not known; wires that end beside it: multiplexer_1_out, CLK_out, registerfile_1_p3, registerfile_1_p4, IF_ID_OP_q[25:21], IF_ID_OP_q[20:16], registerfile_1_p7, registerfile_1_p8
  Multiplexer #(.select(2), .width(32), .enable("false")) multiplexer_4 (
    .in0(registerfile_1_p7), .in1(mips_alu_1_p5), .in2(multiplexer_7_out), .out(multiplexer_4_out),
    .sel(fwd_stall_unit_1_fwd_a));  // open: in3
  Multiplexer #(.select(2), .width(32), .enable("false")) multiplexer_5 (
    .in0(registerfile_1_p8), .in1(mips_alu_1_p5), .in2(multiplexer_7_out), .out(multiplexer_5_out),
    .sel(fwd_stall_unit_1_fwd_b));  // open: in3
  NEXT_PC next_pc_1 (
    .PC(IF_ID_PC_q), .ADDR({IF_ID_OP_q[25:11], IF_ID_OP_q_2, IF_ID_OP_q[5:0]}), .A(multiplexer_4_out),
    .B(multiplexer_5_out), .JB_CTRL(main_ctrl_1_jb_ctrl), .Address(next_pc_1_address),
    .PC_Src(next_pc_1_pc_src));
  Register #(.width(32), .trigger("falling")) ID_EX_A (
    .D(multiplexer_4_out), .en(1'b1), .clk(CLK_out), .Q(ID_EX_A_q));  // open: clr
  Register #(.width(32), .trigger("falling")) ID_EX_B (
    .D(multiplexer_5_out), .en(1'b1), .clk(CLK_out), .Q(ID_EX_B_q));  // open: clr
  Register #(.width(5), .trigger("falling")) ID_EX_RW (
    .D(multiplexer_2_out), .en(1'b1), .clk(CLK_out), .Q(ID_EX_RW_q));  // open: clr
  Register #(.width(5), .trigger("falling")) ID_EX_SA (
    .D(IF_ID_OP_q_2), .en(1'b1), .clk(CLK_out), .Q(ID_EX_SA_q));  // open: clr
  Register #(.width(16), .trigger("falling")) ID_EX_IMM (
    .D({IF_ID_OP_q[15:11], IF_ID_OP_q_2, IF_ID_OP_q[5:0]}), .en(1'b1), .clk(CLK_out), .Q(ID_EX_IMM_q));  // open: clr
  REG_FUNCT_OP reg_funct_op_1 (
    .FUNCT_IN(IF_ID_OP_q[5:0]), .OPCODE_IN(IF_ID_OP_q[31:26]), .CLK(CLK_out),
    .FUNCT_OUT(reg_funct_op_1_funct_out), .OPCODE_OUT(reg_funct_op_1_opcode_out));
  REG_EX reg_ex_1 (
    .ExtOp_IN(main_ctrl_1_extop), .ALUSrc_IN(main_ctrl_1_alusrc), .CLK(CLK_out),
    .ExtOp_OUT(reg_ex_1_extop_out), .ALUSrc_OUT(reg_ex_1_alusrc_out));
  REG_MEM reg_mem_1 (
    .MemRead_IN(main_ctrl_1_memread), .MemWrite_IN(main_ctrl_1_memwrite), .MemToReg_IN(main_ctrl_1_memtoreg),
    .CLK(CLK_out), .MemRead_OUT(reg_mem_1_memread_out), .MemWrite_OUT(reg_mem_1_memwrite_out),
    .MemToReg_OUT(reg_mem_1_memtoreg_out));
  REG_WB reg_wb_1 (.RegWrite_IN(main_ctrl_1_regwrite), .CLK(CLK_out), .RegWrite_OUT(reg_wb_1_regwrite_out));
  Multiplexer #(.width(32), .enable("false")) multiplexer_6 (
    .in0(ID_EX_B_q), .in1(bit_extender_1_out_32b), .out(multiplexer_6_out), .sel(reg_ex_1_alusrc_out));
  BIT_EXTENDER bit_extender_1 (.IN_16b(ID_EX_IMM_q), .ExtOp(reg_ex_1_extop_out), .OUT_32b(bit_extender_1_out_32b));
  ALU_CTRL alu_ctrl_1 (
    .FUNCT(reg_funct_op_1_funct_out), .OPCODE(reg_funct_op_1_opcode_out), .ALU_CTRL(alu_ctrl_1_alu_ctrl));
  // Mips_ALU mips_alu_1: pin names not known; wires that end beside it: ID_EX_A_q, multiplexer_6_out, alu_ctrl_1_alu_ctrl, ID_EX_SA_q, mips_alu_1_p5
  Register #(.width(32), .trigger("falling")) EX_MEM_ALU_Result (
    .D(mips_alu_1_p5), .en(1'b1), .clk(CLK_out), .Q(EX_MEM_ALU_Result_q));  // open: clr
  Register #(.width(32), .trigger("falling")) EX_MEM_DATA_IN (
    .D(ID_EX_B_q), .en(1'b1), .clk(CLK_out), .Q(EX_MEM_DATA_IN_q));  // open: clr
  Register #(.width(5), .trigger("falling")) EX_MEM_RW (
    .D(ID_EX_RW_q), .en(1'b1), .clk(CLK_out), .Q(EX_MEM_RW_q));  // open: clr
  REG_MEM reg_mem_2 (
    .MemRead_IN(reg_mem_1_memread_out), .MemWrite_IN(reg_mem_1_memwrite_out),
    .MemToReg_IN(reg_mem_1_memtoreg_out), .CLK(CLK_out), .MemRead_OUT(reg_mem_2_memread_out),
    .MemWrite_OUT(reg_mem_2_memwrite_out), .MemToReg_OUT(reg_mem_2_memtoreg_out));
  REG_WB reg_wb_2 (.RegWrite_IN(reg_wb_1_regwrite_out), .CLK(CLK_out), .RegWrite_OUT(reg_wb_2_regwrite_out));
  // MIPS_RAM #(.addrWidth(24)) mips_ram_1: pin names not known; wires that end beside it: EX_MEM_ALU_Result_q[23:0], EX_MEM_DATA_IN_q, reg_mem_2_memwrite_out, CLK_out, reg_mem_2_memread_out, RAM_CLEAR, mips_ram_1_p7
  Register #(.width(32), .trigger("falling")) MEM_WB_WriteData (
    .D(multiplexer_7_out), .en(1'b1), .clk(CLK_out), .Q(MEM_WB_WriteData_q));  // open: clr
  Multiplexer #(.width(32), .enable("false")) multiplexer_7 (
    .in0(EX_MEM_ALU_Result_q), .in1(mips_ram_1_p7), .out(multiplexer_7_out), .sel(reg_mem_2_memtoreg_out));
  Register #(.width(5), .trigger("falling")) MEM_WB_RW (
    .D(EX_MEM_RW_q), .en(1'b1), .clk(CLK_out), .Q(registerfile_1_p4));  // open: clr
  REG_WB reg_wb_3 (.RegWrite_IN(reg_wb_2_regwrite_out), .CLK(CLK_out), .RegWrite_OUT(registerfile_1_p3));

  // Notes on the sheet:
  //   contents of mipsprogramrom_1 (hex, n*v repeats v):
  //   addiu $5, $0, 0x5555 addu $6, $5, $4 subu $7, $5, $4 addiu $8, $0, 0x8888 addiu $9, $0, 0x9999 sw
  //   $4, 0($0) lw $3, 0($0) subu $8, $3, $7 addu $7, $5, $6 addiu $10, $0, 0xaaaa beq $0, $0, BRANCH
  //   addiu $1, $1, 0x1111 addiu $1, $1, 0xffff BRANCH: addiu $2, $0, 0x2222
endmodule

module PC (
  input  JR,
  input  [31:0] REG_BUS,
  input  PC_SRC,
  input  [29:0] ADDR,
  input  PC_RESET,
  input  CLK,
  input  PC_Write,
  output [29:0] PC_INCR_30b,
  output [31:0] PC
);

  wire not_1_out;
  wire [29:0] multiplexer_1_out, multiplexer_2_out;

  not not_1 (not_1_out, JR);
  Multiplexer #(.width(30), .enable("false")) multiplexer_1 (
    .in0(REG_BUS[31:2]), .in1(multiplexer_2_out), .out(multiplexer_1_out), .sel(not_1_out));
  Multiplexer #(.width(30), .enable("false")) multiplexer_2 (
    .in0(PC_INCR_30b), .in1(ADDR), .out(multiplexer_2_out), .sel(PC_SRC));
  Register #(.width(32), .trigger("falling")) register_1 (
    .D({multiplexer_1_out, 2'b00}), .en(PC_Write), .clk(CLK), .Q(PC), .clr(PC_RESET));
  // Incrementer #(.width(30)) incrementer_1: pin names not known; wires that end beside it: PC[31:2], PC_INCR_30b
endmodule

module MAIN_CTRL (
  input  [5:0] OPCODE,
  input  Bubble,
  output RegWrite,
  output ExtOp,
  output MemRead,
  output MemWrite,
  output MemToReg,
  output ALUSrc,
  output [2:0] JB_CTRL,
  output Link
);

  wire and_1_out, and_2_out, and_3_out, and_4_out, and_5_out, and_6_out, and_7_out, and_8_out, and_9_out,
       not_1_out, not_2_out, not_3_out, not_4_out, not_5_out, not_6_out, not_7_out, not_8_out, not_9_out,
       not_10_out, not_11_out, not_12_out, not_13_out, not_14_out, or_1_out, or_2_out, or_3_out;

  not not_1 (not_1_out, Bubble);
  not not_2 (not_2_out, OPCODE[2]);
  not not_3 (not_3_out, OPCODE[1]);
  not not_4 (not_4_out, OPCODE[3]);
  not not_5 (not_5_out, OPCODE[2]);
  not not_6 (not_6_out, OPCODE[5]);
  not not_7 (not_7_out, OPCODE[3]);
  and and_1 (and_1_out, OPCODE[5], OPCODE[3]);
  or or_1 (or_1_out, OPCODE[1], OPCODE[3]);
  not not_8 (not_8_out, OPCODE[5]);
  not not_9 (not_9_out, OPCODE[3]);
  not not_10 (not_10_out, OPCODE[3]);
  not not_11 (not_11_out, OPCODE[0]);
  not not_12 (not_12_out, OPCODE[3]);
  not not_13 (not_13_out, OPCODE[1]);
  not not_14 (not_14_out, OPCODE[5]);
  and and_2 (and_2_out, not_2_out, not_3_out);
  and and_3 (and_3_out, not_4_out, not_5_out, OPCODE[0]);
  and and_4 (and_4_out, not_6_out, OPCODE[3]);
  and and_5 (and_5_out, not_7_out, OPCODE[2]);
  and and_6 (and_6_out, not_8_out, not_9_out, OPCODE[1]);
  and and_7 (and_7_out, not_10_out, OPCODE[2], not_11_out);
  and and_8 (and_8_out, not_12_out, not_13_out, OPCODE[0]);
  and and_9 (and_9_out, not_14_out, OPCODE[1], OPCODE[0]);
  or or_2 (or_2_out, and_2_out, and_3_out, and_4_out);
  or or_3 (or_3_out, and_5_out, OPCODE[5]);
  and and_10 (RegWrite, or_2_out, not_1_out);
  and and_11 (ExtOp, or_3_out, not_1_out);
  and and_12 (MemRead, OPCODE[5], not_1_out);
  and and_13 (MemWrite, and_1_out, not_1_out);
  and and_14 (MemToReg, OPCODE[5], not_1_out);
  and and_15 (ALUSrc, or_1_out, not_1_out);
  and and_16 (JB_CTRL[2], and_6_out, not_1_out);
  and and_17 (JB_CTRL[1], and_7_out, not_1_out);
  and and_18 (JB_CTRL[0], and_8_out, not_1_out);
  and and_19 (Link, and_9_out, not_1_out);

  // Notes on the sheet:
  //   2 - j
  //   1 - beq
  //   0 - bne
endmodule

module ALU_CTRL (
  input  [5:0] FUNCT,
  input  [5:0] OPCODE,
  output [3:0] ALU_CTRL
);

  wire or_1_out;
  wire [3:0] ij_type_alu_ctrl_1_alu_ctrl, r_type_alu_ctrl_1_alu_ctrl;

  or or_1 (or_1_out, OPCODE[0], OPCODE[1], OPCODE[2], OPCODE[3], OPCODE[4], OPCODE[5]);
  R_TYPE_ALU_CTRL r_type_alu_ctrl_1 (.FUNCT(FUNCT), .ALU_CTRL(r_type_alu_ctrl_1_alu_ctrl));
  IJ_TYPE_ALU_CTRL ij_type_alu_ctrl_1 (.OPCODE(OPCODE), .ALU_CTRL(ij_type_alu_ctrl_1_alu_ctrl));
  Multiplexer #(.width(4), .enable("false")) multiplexer_1 (
    .in0(r_type_alu_ctrl_1_alu_ctrl), .in1(ij_type_alu_ctrl_1_alu_ctrl), .out(ALU_CTRL), .sel(or_1_out));
endmodule

module R_TYPE_ALU_CTRL (
  input  [5:0] FUNCT,
  output [3:0] ALU_CTRL
);

  wire not_1_out;

  and and_1 (ALU_CTRL[1], FUNCT[5], FUNCT[0]);
  not not_1 (not_1_out, FUNCT[5]);
  and and_2 (ALU_CTRL[0], not_1_out, FUNCT[0]);

  assign ALU_CTRL[3:2] = FUNCT[2:1];
endmodule

module IJ_TYPE_ALU_CTRL (
  input  [5:0] OPCODE,
  output [3:0] ALU_CTRL
);

  wire and_2_out, and_3_out, not_1_out, not_2_out, not_3_out, not_4_out;

  and and_1 (ALU_CTRL[3], OPCODE[3], OPCODE[2]);
  not not_1 (not_1_out, OPCODE[3]);
  not not_2 (not_2_out, OPCODE[1]);
  not not_3 (not_3_out, OPCODE[0]);
  not not_4 (not_4_out, OPCODE[3]);
  and and_2 (and_2_out, not_1_out, not_2_out);
  and and_3 (and_3_out, OPCODE[1], not_3_out);
  or or_1 (ALU_CTRL[1], not_4_out, OPCODE[0]);
  or or_2 (ALU_CTRL[2], and_2_out, and_3_out);

  assign ALU_CTRL[0] = 1'b0;
endmodule

module NEXT_PC (
  input  [29:0] PC,
  input  [25:0] ADDR,
  input  [31:0] A,
  input  [31:0] B,
  input  [2:0] JB_CTRL,
  output [29:0] Address,
  output PC_Src
);

  wire and_1_out, and_2_out, comparator_1_eq;
  wire [29:0] adder_1_out, bit_extender_1_out;

  assign bit_extender_1_out = {{14{1'b0}}, ADDR[15:0]};  // Bit_Extender bit_extender_1
  Adder #(.width(30)) adder_1 (.a(PC), .b(bit_extender_1_out), .out(adder_1_out));  // open: cin, cout
  Multiplexer #(.width(30), .enable("false")) multiplexer_1 (
    .in0(adder_1_out), .in1({PC[29:26], ADDR}), .out(Address), .sel(JB_CTRL[2]));
  or or_1 (PC_Src, and_1_out, JB_CTRL[2], and_2_out);
  and and_1 (and_1_out, comparator_1_eq, JB_CTRL[1]);
  Comparator #(.width(32)) comparator_1 (.a(A), .b(B), .eq(comparator_1_eq));  // open: gt, lt
  and and_2 (and_2_out, ~comparator_1_eq, JB_CTRL[0]);  // AND_Gate

  // Notes on the sheet:
  //   2 - j
  //   0 - bne
  //   1 - beq
endmodule

module R_TYPE_TEST (
  input  [5:0] OPCODE,
  output R_TYPE
);

  nor nor_1 (R_TYPE, OPCODE[0], OPCODE[1], OPCODE[2], OPCODE[3], OPCODE[4], OPCODE[5]);
endmodule

module JR_HANDLE (
  input  [5:0] FUNCT,
  input  R_TYPE,
  output JR
);

  and and_1 (JR, ~FUNCT[5], ~FUNCT[4], FUNCT[3], ~FUNCT[2], ~FUNCT[1], ~FUNCT[0], R_TYPE);  // AND_Gate
endmodule

module BIT_EXTENDER (
  input  [15:0] IN_16b,
  input  ExtOp,
  output [31:0] OUT_32b
);

  wire and_1_out;

  and and_1 (and_1_out, IN_16b[15], ExtOp);
  assign OUT_32b = {{16{and_1_out}}, IN_16b};  // Bit_Extender bit_extender_1
endmodule

module REG_EX (
  input  ExtOp_IN,
  input  ALUSrc_IN,
  input  CLK,
  output ExtOp_OUT,
  output ALUSrc_OUT
);

  Register #(.width(1), .trigger("falling")) ExtOp (.D(ExtOp_IN), .en(1'b1), .clk(CLK), .Q(ExtOp_OUT));  // open: clr
  Register #(.width(1), .trigger("falling")) ALUSrc (.D(ALUSrc_IN), .en(1'b1), .clk(CLK), .Q(ALUSrc_OUT));  // open: clr
endmodule

module REG_MEM (
  input  MemRead_IN,
  input  MemWrite_IN,
  input  MemToReg_IN,
  input  CLK,
  output MemRead_OUT,
  output MemWrite_OUT,
  output MemToReg_OUT
);

  Register #(.width(1), .trigger("falling")) MemRead (
    .D(MemRead_IN), .en(1'b1), .clk(CLK), .Q(MemRead_OUT));  // open: clr
  Register #(.width(1), .trigger("falling")) MemWrite (
    .D(MemWrite_IN), .en(1'b1), .clk(CLK), .Q(MemWrite_OUT));  // open: clr
  Register #(.width(1), .trigger("falling")) MemToReg (
    .D(MemToReg_IN), .en(1'b1), .clk(CLK), .Q(MemToReg_OUT));  // open: clr
endmodule

module REG_WB (
  input  RegWrite_IN,
  input  CLK,
  output RegWrite_OUT
);

  Register #(.width(1), .trigger("falling")) RegWrite (
    .D(RegWrite_IN), .en(1'b1), .clk(CLK), .Q(RegWrite_OUT));  // open: clr
endmodule

module REG_FUNCT_OP (
  input  [5:0] FUNCT_IN,
  input  [5:0] OPCODE_IN,
  input  CLK,
  output [5:0] FUNCT_OUT,
  output [5:0] OPCODE_OUT
);

  Register #(.width(6), .trigger("falling")) FUNCT (.D(FUNCT_IN), .en(1'b1), .clk(CLK), .Q(FUNCT_OUT));  // open: clr
  Register #(.width(6), .trigger("falling")) OPCODE (.D(OPCODE_IN), .en(1'b1), .clk(CLK), .Q(OPCODE_OUT));  // open: clr
endmodule

module Forwarding_Unit (
  input  [4:0] RS_ID,
  input  [4:0] RT_ID,
  input  [4:0] RW_EX,
  input  [4:0] RW_MEM,
  output [1:0] FWD_A,
  output [1:0] FWD_B
);

  Comparator #(.width(5)) comparator_1 (.a(RS_ID), .b(RW_EX), .eq(FWD_A[0]));  // open: gt, lt
  Comparator #(.width(5)) comparator_2 (.a(RT_ID), .b(RW_EX), .eq(FWD_B[0]));  // open: gt, lt
  Comparator #(.width(5)) comparator_3 (.a(RW_MEM), .b(RS_ID), .eq(FWD_A[1]));  // open: gt, lt
  Comparator #(.width(5)) comparator_4 (.a(RW_MEM), .b(RT_ID), .eq(FWD_B[1]));  // open: gt, lt
endmodule

module Stall_Unit (
  input  [4:0] RS_ID,
  input  [4:0] RT_ID,
  input  [4:0] RW_EX,
  input  MemRead_EX,
  output PC_Write,
  output IF_ID_Write,
  output Bubble
);

  wire comparator_1_eq, comparator_2_eq, comparator_3_eq, not_1_out, or_1_out;

  Comparator #(.width(5)) comparator_1 (.a(RS_ID), .b(RW_EX), .eq(comparator_1_eq));  // open: gt, lt
  Comparator #(.width(5)) comparator_2 (.a(RT_ID), .b(RW_EX), .eq(comparator_2_eq));  // open: gt, lt
  Comparator #(.width(5)) comparator_3 (.a(RW_EX), .b({5{1'b0}}), .eq(comparator_3_eq));  // open: gt, lt
  or or_1 (or_1_out, comparator_1_eq, comparator_2_eq);
  not not_1 (not_1_out, comparator_3_eq);
  and and_1 (Bubble, or_1_out, not_1_out, MemRead_EX);
  not not_2 (IF_ID_Write, Bubble);

  assign PC_Write = IF_ID_Write;
endmodule

module FWD_STALL_UNIT (
  input  [4:0] RS_ID,
  input  [4:0] RT_ID,
  input  [4:0] RW_EX,
  input  [4:0] RW_MEM,
  input  MemRead_EX,
  output [1:0] FWD_A,
  output [1:0] FWD_B,
  output PC_Write,
  output IF_ID_Write,
  output Bubble
);

  Forwarding_Unit forwarding_unit_1 (
    .RS_ID(RS_ID), .RT_ID(RT_ID), .RW_EX(RW_EX), .RW_MEM(RW_MEM), .FWD_A(FWD_A), .FWD_B(FWD_B));
  Stall_Unit stall_unit_1 (
    .RS_ID(RS_ID), .RT_ID(RT_ID), .RW_EX(RW_EX), .MemRead_EX(MemRead_EX), .PC_Write(PC_Write),
    .IF_ID_Write(IF_ID_Write), .Bubble(Bubble));
endmodule
