// Logisim project components.circ as structural Verilog
module RS_Latch (
  input  R,
  input  S,
  output Q,
  output NQ
);

  nor nor_1 (Q, R, NQ);
  nor nor_2 (NQ, Q, S);
endmodule

module D_Latch (
  input  CLK,
  input  D,
  output Q,
  output NQ
);

  wire and_1_out, and_2_out;

  and and_1 (and_1_out, CLK, ~D);  // AND_Gate
  and and_2 (and_2_out, CLK, D);
  RS_Latch rs_latch_1 (.R(and_1_out), .S(and_2_out), .Q(Q), .NQ(NQ));
endmodule

module D_FlipFlop (
  input  D,
  input  CLK,
  input  WE,
  output Q,
  output NQ
);

  wire d_latch_1_q, multiplexer_1_out, not_1_out;

  Multiplexer #(.enable("false")) multiplexer_1 (.in0(Q), .in1(D), .out(multiplexer_1_out), .sel(WE));
  D_Latch d_latch_1 (.CLK(CLK), .D(multiplexer_1_out), .Q(d_latch_1_q));  // open: NQ
  not not_1 (not_1_out, CLK);
  D_Latch d_latch_2 (.CLK(not_1_out), .D(d_latch_1_q), .Q(Q), .NQ(NQ));
endmodule

module Register_1b (
  input  D_in,
  input  CLK,
  input  WE,
  output D_out
);

  D_FlipFlop d_flipflop_1 (.D(D_in), .CLK(CLK), .WE(WE), .Q(D_out));  // open: NQ
endmodule

module Register_2b (
  input  [1:0] D_in,
  input  CLK,
  input  WE,
  output [1:0] D_out
);

  Register_1b register_1b_1 (.D_in(D_in[0]), .CLK(CLK), .WE(WE), .D_out(D_out[0]));
  Register_1b register_1b_2 (.D_in(D_in[1]), .CLK(CLK), .WE(WE), .D_out(D_out[1]));
endmodule

module Register_4b (
  input  [3:0] D_in,
  input  CLK,
  input  WE,
  output [3:0] D_out
);

  Register_2b register_2b_1 (.D_in(D_in[1:0]), .CLK(CLK), .WE(WE), .D_out(D_out[1:0]));
  Register_2b register_2b_2 (.D_in(D_in[3:2]), .CLK(CLK), .WE(WE), .D_out(D_out[3:2]));
endmodule

module Register_8b (
  input  [7:0] D_in,
  input  CLK,
  input  WE,
  output [7:0] D_out
);

  Register_4b register_4b_1 (.D_in(D_in[3:0]), .CLK(CLK), .WE(WE), .D_out(D_out[3:0]));
  Register_4b register_4b_2 (.D_in(D_in[7:4]), .CLK(CLK), .WE(WE), .D_out(D_out[7:4]));
endmodule

module Register_16b (
  input  [15:0] D_in,
  input  CLK,
  input  WE,
  output [15:0] D_out
);

  Register_8b register_8b_1 (.D_in(D_in[7:0]), .CLK(CLK), .WE(WE), .D_out(D_out[7:0]));
  Register_8b register_8b_2 (.D_in(D_in[15:8]), .CLK(CLK), .WE(WE), .D_out(D_out[15:8]));
endmodule

module Register_32b (
  input  [31:0] D_in,
  input  CLK,
  input  WE,
  output [31:0] D_out
);

  Register_16b register_16b_1 (.D_in(D_in[15:0]), .CLK(CLK), .WE(WE), .D_out(D_out[15:0]));
  Register_16b register_16b_2 (.D_in(D_in[31:16]), .CLK(CLK), .WE(WE), .D_out(D_out[31:16]));
endmodule

module Adder_1b (
  input  A,
  input  B,
  input  Cin,
  output Cout,
  output R
);

  wire and_1_out, and_2_out, and_3_out, and_4_out, and_5_out, and_6_out, and_7_out, not_1_out, not_2_out,
       not_3_out, not_4_out, not_5_out, not_6_out;

  and and_1 (and_1_out, B, Cin);
  and and_2 (and_2_out, A, Cin);
  and and_3 (and_3_out, A, B);
  not not_1 (not_1_out, A);
  not not_2 (not_2_out, B);
  not not_3 (not_3_out, A);
  not not_4 (not_4_out, Cin);
  not not_5 (not_5_out, B);
  not not_6 (not_6_out, Cin);
  or or_1 (Cout, and_1_out, and_2_out, and_3_out);
  and and_4 (and_4_out, not_1_out, not_2_out, Cin);
  and and_5 (and_5_out, not_3_out, B, not_4_out);
  and and_6 (and_6_out, A, not_5_out, not_6_out);
  and and_7 (and_7_out, A, B, Cin);
  or or_2 (R, and_4_out, and_5_out, and_6_out, and_7_out);
endmodule

module Adder_2b (
  input  [1:0] A,
  input  [1:0] B,
  input  Cin,
  output Cout,
  output [1:0] R
);

  wire adder_1b_2_cout;

  Adder_1b adder_1b_1 (.A(A[1]), .B(B[1]), .Cin(adder_1b_2_cout), .Cout(Cout), .R(R[1]));
  Adder_1b adder_1b_2 (.A(A[0]), .B(B[0]), .Cin(Cin), .Cout(adder_1b_2_cout), .R(R[0]));
endmodule

module Adder_4b (
  input  [3:0] A,
  input  [3:0] B,
  input  Cin,
  output Cout,
  output [3:0] R
);

  wire adder_2b_2_cout;

  Adder_2b adder_2b_1 (.A(A[3:2]), .B(B[3:2]), .Cin(adder_2b_2_cout), .Cout(Cout), .R(R[3:2]));
  Adder_2b adder_2b_2 (.A(A[1:0]), .B(B[1:0]), .Cin(Cin), .Cout(adder_2b_2_cout), .R(R[1:0]));
endmodule

module Adder_8b (
  input  [7:0] A,
  input  [7:0] B,
  input  Cin,
  output Cout,
  output [7:0] R
);

  wire adder_4b_2_cout;

  Adder_4b adder_4b_1 (.A(A[7:4]), .B(B[7:4]), .Cin(adder_4b_2_cout), .Cout(Cout), .R(R[7:4]));
  Adder_4b adder_4b_2 (.A(A[3:0]), .B(B[3:0]), .Cin(Cin), .Cout(adder_4b_2_cout), .R(R[3:0]));
endmodule

module Adder_16b (
  input  [15:0] A,
  input  [15:0] B,
  input  Cin,
  output Cout,
  output [15:0] R
);

  wire adder_8b_2_cout;

  Adder_8b adder_8b_1 (.A(A[15:8]), .B(B[15:8]), .Cin(adder_8b_2_cout), .Cout(Cout), .R(R[15:8]));
  Adder_8b adder_8b_2 (.A(A[7:0]), .B(B[7:0]), .Cin(Cin), .Cout(adder_8b_2_cout), .R(R[7:0]));
endmodule

module Adder_32b (
  input  [31:0] A,
  input  [31:0] B,
  input  Cin,
  output Cout,
  output [31:0] R
);

  wire adder_16b_2_cout;

  Adder_16b adder_16b_1 (.A(A[31:16]), .B(B[31:16]), .Cin(adder_16b_2_cout), .Cout(Cout), .R(R[31:16]));
  Adder_16b adder_16b_2 (.A(A[15:0]), .B(B[15:0]), .Cin(Cin), .Cout(adder_16b_2_cout), .R(R[15:0]));
endmodule

module RegisterFile_2R_WZ (
  input  RA,
  input  RB,
  input  RW,
  input  CLK,
  input  RegWrite,
  input  [31:0] BusW,
  output [31:0] BusA,
  output [31:0] BusB
);

  wire and_1_out, decoder_1_out1;
  wire [31:0] register_32b_1_d_out;

  Decoder #(.enable("false")) decoder_1 (.out1(decoder_1_out1), .sel(RW));  // open: out0
  and and_1 (and_1_out, decoder_1_out1, RegWrite);
  Register_32b register_32b_1 (.D_in(BusW), .CLK(CLK), .WE(and_1_out), .D_out(register_32b_1_d_out));
  Multiplexer #(.width(32), .enable("false")) multiplexer_1 (
    .in0({32{1'b0}}), .in1(register_32b_1_d_out), .out(BusA), .sel(RA));
  Multiplexer #(.width(32), .enable("false")) multiplexer_2 (
    .in0({32{1'b0}}), .in1(register_32b_1_d_out), .out(BusB), .sel(RB));
endmodule

module RegisterFile_2R_NZ (
  input  RA,
  input  RB,
  input  RW,
  input  CLK,
  input  RegWrite,
  input  [31:0] BusW,
  output [31:0] BusA,
  output [31:0] BusB
);

  wire and_1_out, and_2_out, decoder_1_out0, decoder_1_out1;
  wire [31:0] register_32b_1_d_out, register_32b_2_d_out;

  Decoder #(.enable("false")) decoder_1 (.out0(decoder_1_out0), .out1(decoder_1_out1), .sel(RW));
  and and_1 (and_1_out, decoder_1_out0, RegWrite);
  and and_2 (and_2_out, decoder_1_out1, RegWrite);
  Register_32b register_32b_1 (.D_in(BusW), .CLK(CLK), .WE(and_1_out), .D_out(register_32b_1_d_out));
  Register_32b register_32b_2 (.D_in(BusW), .CLK(CLK), .WE(and_2_out), .D_out(register_32b_2_d_out));
  Multiplexer #(.width(32), .enable("false")) multiplexer_1 (
    .in0(register_32b_1_d_out), .in1(register_32b_2_d_out), .out(BusA), .sel(RA));
  Multiplexer #(.width(32), .enable("false")) multiplexer_2 (
    .in0(register_32b_1_d_out), .in1(register_32b_2_d_out), .out(BusB), .sel(RB));
endmodule

module RegisterFile_4R_WZ (
  input  [1:0] RA,
  input  [1:0] RB,
  input  [1:0] RW,
  input  CLK,
  input  RegWrite,
  input  [31:0] BusW,
  output [31:0] BusA,
  output [31:0] BusB
);

  wire and_1_out, and_2_out, demultiplexer_1_out0, demultiplexer_1_out1, demultiplexer_2_out0,
       demultiplexer_2_out1, demultiplexer_3_out0, demultiplexer_3_out1;
  wire [31:0] registerfile_2r_nz_1_busa, registerfile_2r_nz_1_busb, registerfile_2r_wz_1_busa,
       registerfile_2r_wz_1_busb;

  Demultiplexer #(.enable("false")) demultiplexer_1 (
    .out0(demultiplexer_1_out0), .out1(demultiplexer_1_out1), .in(RW[0]), .sel(RW[1]));
  Demultiplexer #(.enable("false")) demultiplexer_2 (
    .out0(demultiplexer_2_out0), .out1(demultiplexer_2_out1), .in(RB[0]), .sel(RB[1]));
  Demultiplexer #(.enable("false")) demultiplexer_3 (
    .out0(demultiplexer_3_out0), .out1(demultiplexer_3_out1), .in(RA[0]), .sel(RA[1]));
  and and_1 (and_1_out, ~RW[1], RegWrite);  // AND_Gate
  and and_2 (and_2_out, RW[1], RegWrite);
  RegisterFile_2R_WZ registerfile_2r_wz_1 (
    .RA(demultiplexer_3_out0), .RB(demultiplexer_2_out0), .RW(demultiplexer_1_out0), .CLK(CLK),
    .RegWrite(and_1_out), .BusW(BusW), .BusA(registerfile_2r_wz_1_busa), .BusB(registerfile_2r_wz_1_busb));
  RegisterFile_2R_NZ registerfile_2r_nz_1 (
    .RA(demultiplexer_3_out1), .RB(demultiplexer_2_out1), .RW(demultiplexer_1_out1), .CLK(CLK),
    .RegWrite(and_2_out), .BusW(BusW), .BusA(registerfile_2r_nz_1_busa), .BusB(registerfile_2r_nz_1_busb));
  Multiplexer #(.width(32), .enable("false")) multiplexer_1 (
    .in0(registerfile_2r_wz_1_busa), .in1(registerfile_2r_nz_1_busa), .out(BusA), .sel(RA[1]));
  Multiplexer #(.width(32), .enable("false")) multiplexer_2 (
    .in0(registerfile_2r_wz_1_busb), .in1(registerfile_2r_nz_1_busb), .out(BusB), .sel(RB[1]));
endmodule

module RegisterFile_4R_NZ (
  input  [1:0] RA,
  input  [1:0] RB,
  input  [1:0] RW,
  input  CLK,
  input  RegWrite,
  input  [31:0] BusW,
  output [31:0] BusA,
  output [31:0] BusB
);

  wire and_1_out, and_2_out, demultiplexer_1_out0, demultiplexer_1_out1, demultiplexer_2_out0,
       demultiplexer_2_out1, demultiplexer_3_out0, demultiplexer_3_out1;
  wire [31:0] registerfile_2r_nz_1_busa, registerfile_2r_nz_1_busb, registerfile_2r_nz_2_busa,
       registerfile_2r_nz_2_busb;

  Demultiplexer #(.enable("false")) demultiplexer_1 (
    .out0(demultiplexer_1_out0), .out1(demultiplexer_1_out1), .in(RW[0]), .sel(RW[1]));
  Demultiplexer #(.enable("false")) demultiplexer_2 (
    .out0(demultiplexer_2_out0), .out1(demultiplexer_2_out1), .in(RB[0]), .sel(RB[1]));
  Demultiplexer #(.enable("false")) demultiplexer_3 (
    .out0(demultiplexer_3_out0), .out1(demultiplexer_3_out1), .in(RA[0]), .sel(RA[1]));
  and and_1 (and_1_out, ~RW[1], RegWrite);  // AND_Gate
  and and_2 (and_2_out, RW[1], RegWrite);
  RegisterFile_2R_NZ registerfile_2r_nz_1 (
    .RA(demultiplexer_3_out0), .RB(demultiplexer_2_out0), .RW(demultiplexer_1_out0), .CLK(CLK),
    .RegWrite(and_1_out), .BusW(BusW), .BusA(registerfile_2r_nz_1_busa), .BusB(registerfile_2r_nz_1_busb));
  RegisterFile_2R_NZ registerfile_2r_nz_2 (
    .RA(demultiplexer_3_out1), .RB(demultiplexer_2_out1), .RW(demultiplexer_1_out1), .CLK(CLK),
    .RegWrite(and_2_out), .BusW(BusW), .BusA(registerfile_2r_nz_2_busa), .BusB(registerfile_2r_nz_2_busb));
  Multiplexer #(.width(32), .enable("false")) multiplexer_1 (
    .in0(registerfile_2r_nz_1_busa), .in1(registerfile_2r_nz_2_busa), .out(BusA), .sel(RA[1]));
  Multiplexer #(.width(32), .enable("false")) multiplexer_2 (
    .in0(registerfile_2r_nz_1_busb), .in1(registerfile_2r_nz_2_busb), .out(BusB), .sel(RB[1]));
endmodule

module RegisterFile_8R_WZ (
  input  [2:0] RA,
  input  [2:0] RB,
  input  [2:0] RW,
  input  CLK,
  input  RegWrite,
  input  [31:0] BusW,
  output [31:0] BusA,
  output [31:0] BusB
);

  wire and_1_out, and_2_out;
  wire [1:0] demultiplexer_1_out0, demultiplexer_1_out1, demultiplexer_2_out0, demultiplexer_2_out1,
       demultiplexer_3_out0, demultiplexer_3_out1;
  wire [31:0] registerfile_4r_nz_1_busa, registerfile_4r_nz_1_busb, registerfile_4r_wz_1_busa,
       registerfile_4r_wz_1_busb;

  Demultiplexer #(.width(2), .enable("false")) demultiplexer_1 (
    .out0(demultiplexer_1_out0), .out1(demultiplexer_1_out1), .in(RW[1:0]), .sel(RW[2]));
  Demultiplexer #(.width(2), .enable("false")) demultiplexer_2 (
    .out0(demultiplexer_2_out0), .out1(demultiplexer_2_out1), .in(RB[1:0]), .sel(RB[2]));
  Demultiplexer #(.width(2), .enable("false")) demultiplexer_3 (
    .out0(demultiplexer_3_out0), .out1(demultiplexer_3_out1), .in(RA[1:0]), .sel(RA[2]));
  and and_1 (and_1_out, ~RW[2], RegWrite);  // AND_Gate
  and and_2 (and_2_out, RW[2], RegWrite);
  RegisterFile_4R_WZ registerfile_4r_wz_1 (
    .RA(demultiplexer_3_out0), .RB(demultiplexer_2_out0), .RW(demultiplexer_1_out0), .CLK(CLK),
    .RegWrite(and_1_out), .BusW(BusW), .BusA(registerfile_4r_wz_1_busa), .BusB(registerfile_4r_wz_1_busb));
  RegisterFile_4R_NZ registerfile_4r_nz_1 (
    .RA(demultiplexer_3_out1), .RB(demultiplexer_2_out1), .RW(demultiplexer_1_out1), .CLK(CLK),
    .RegWrite(and_2_out), .BusW(BusW), .BusA(registerfile_4r_nz_1_busa), .BusB(registerfile_4r_nz_1_busb));
  Multiplexer #(.width(32), .enable("false")) multiplexer_1 (
    .in0(registerfile_4r_wz_1_busa), .in1(registerfile_4r_nz_1_busa), .out(BusA), .sel(RA[2]));
  Multiplexer #(.width(32), .enable("false")) multiplexer_2 (
    .in0(registerfile_4r_wz_1_busb), .in1(registerfile_4r_nz_1_busb), .out(BusB), .sel(RB[2]));
endmodule

module RegisterFile_8R_NZ (
  input  [2:0] RA,
  input  [2:0] RB,
  input  [2:0] RW,
  input  CLK,
  input  RegWrite,
  input  [31:0] BusW,
  output [31:0] BusA,
  output [31:0] BusB
);

  wire and_1_out, and_2_out;
  wire [1:0] demultiplexer_1_out0, demultiplexer_1_out1, demultiplexer_2_out0, demultiplexer_2_out1,
       demultiplexer_3_out0, demultiplexer_3_out1;
  wire [31:0] registerfile_4r_nz_1_busa, registerfile_4r_nz_1_busb, registerfile_4r_nz_2_busa,
       registerfile_4r_nz_2_busb;

  Demultiplexer #(.width(2), .enable("false")) demultiplexer_1 (
    .out0(demultiplexer_1_out0), .out1(demultiplexer_1_out1), .in(RW[1:0]), .sel(RW[2]));
  Demultiplexer #(.width(2), .enable("false")) demultiplexer_2 (
    .out0(demultiplexer_2_out0), .out1(demultiplexer_2_out1), .in(RB[1:0]), .sel(RB[2]));
  Demultiplexer #(.width(2), .enable("false")) demultiplexer_3 (
    .out0(demultiplexer_3_out0), .out1(demultiplexer_3_out1), .in(RA[1:0]), .sel(RA[2]));
  and and_1 (and_1_out, ~RW[2], RegWrite);  // AND_Gate
  and and_2 (and_2_out, RW[2], RegWrite);
  RegisterFile_4R_NZ registerfile_4r_nz_1 (
    .RA(demultiplexer_3_out0), .RB(demultiplexer_2_out0), .RW(demultiplexer_1_out0), .CLK(CLK),
    .RegWrite(and_1_out), .BusW(BusW), .BusA(registerfile_4r_nz_1_busa), .BusB(registerfile_4r_nz_1_busb));
  RegisterFile_4R_NZ registerfile_4r_nz_2 (
    .RA(demultiplexer_3_out1), .RB(demultiplexer_2_out1), .RW(demultiplexer_1_out1), .CLK(CLK),
    .RegWrite(and_2_out), .BusW(BusW), .BusA(registerfile_4r_nz_2_busa), .BusB(registerfile_4r_nz_2_busb));
  Multiplexer #(.width(32), .enable("false")) multiplexer_1 (
    .in0(registerfile_4r_nz_1_busa), .in1(registerfile_4r_nz_2_busa), .out(BusA), .sel(RA[2]));
  Multiplexer #(.width(32), .enable("false")) multiplexer_2 (
    .in0(registerfile_4r_nz_1_busb), .in1(registerfile_4r_nz_2_busb), .out(BusB), .sel(RB[2]));
endmodule

module RegisterFile_16R_WZ (
  input  [3:0] RA,
  input  [3:0] RB,
  input  [3:0] RW,
  input  CLK,
  input  RegWrite,
  input  [31:0] BusW,
  output [31:0] BusA,
  output [31:0] BusB
);

  wire and_1_out, and_2_out;
  wire [2:0] demultiplexer_1_out0, demultiplexer_1_out1, demultiplexer_2_out0, demultiplexer_2_out1,
       demultiplexer_3_out0, demultiplexer_3_out1;
  wire [31:0] registerfile_8r_nz_1_busa, registerfile_8r_nz_1_busb, registerfile_8r_wz_1_busa,
       registerfile_8r_wz_1_busb;

  Demultiplexer #(.width(3), .enable("false")) demultiplexer_1 (
    .out0(demultiplexer_1_out0), .out1(demultiplexer_1_out1), .in(RW[2:0]), .sel(RW[3]));
  Demultiplexer #(.width(3), .enable("false")) demultiplexer_2 (
    .out0(demultiplexer_2_out0), .out1(demultiplexer_2_out1), .in(RB[2:0]), .sel(RB[3]));
  Demultiplexer #(.width(3), .enable("false")) demultiplexer_3 (
    .out0(demultiplexer_3_out0), .out1(demultiplexer_3_out1), .in(RA[2:0]), .sel(RA[3]));
  and and_1 (and_1_out, ~RW[3], RegWrite);  // AND_Gate
  and and_2 (and_2_out, RW[3], RegWrite);
  RegisterFile_8R_WZ registerfile_8r_wz_1 (
    .RA(demultiplexer_3_out0), .RB(demultiplexer_2_out0), .RW(demultiplexer_1_out0), .CLK(CLK),
    .RegWrite(and_1_out), .BusW(BusW), .BusA(registerfile_8r_wz_1_busa), .BusB(registerfile_8r_wz_1_busb));
  RegisterFile_8R_NZ registerfile_8r_nz_1 (
    .RA(demultiplexer_3_out1), .RB(demultiplexer_2_out1), .RW(demultiplexer_1_out1), .CLK(CLK),
    .RegWrite(and_2_out), .BusW(BusW), .BusA(registerfile_8r_nz_1_busa), .BusB(registerfile_8r_nz_1_busb));
  Multiplexer #(.width(32), .enable("false")) multiplexer_1 (
    .in0(registerfile_8r_wz_1_busa), .in1(registerfile_8r_nz_1_busa), .out(BusA), .sel(RA[3]));
  Multiplexer #(.width(32), .enable("false")) multiplexer_2 (
    .in0(registerfile_8r_wz_1_busb), .in1(registerfile_8r_nz_1_busb), .out(BusB), .sel(RB[3]));
endmodule

module RegisterFile_16R_NZ (
  input  [3:0] RA,
  input  [3:0] RB,
  input  [3:0] RW,
  input  CLK,
  input  RegWrite,
  input  [31:0] BusW,
  output [31:0] BusA,
  output [31:0] BusB
);

  wire and_1_out, and_2_out;
  wire [2:0] demultiplexer_1_out0, demultiplexer_1_out1, demultiplexer_2_out0, demultiplexer_2_out1,
       demultiplexer_3_out0, demultiplexer_3_out1;
  wire [31:0] registerfile_8r_nz_1_busa, registerfile_8r_nz_1_busb, registerfile_8r_nz_2_busa,
       registerfile_8r_nz_2_busb;

  Demultiplexer #(.width(3), .enable("false")) demultiplexer_1 (
    .out0(demultiplexer_1_out0), .out1(demultiplexer_1_out1), .in(RW[2:0]), .sel(RW[3]));
  Demultiplexer #(.width(3), .enable("false")) demultiplexer_2 (
    .out0(demultiplexer_2_out0), .out1(demultiplexer_2_out1), .in(RB[2:0]), .sel(RB[3]));
  Demultiplexer #(.width(3), .enable("false")) demultiplexer_3 (
    .out0(demultiplexer_3_out0), .out1(demultiplexer_3_out1), .in(RA[2:0]), .sel(RA[3]));
  and and_1 (and_1_out, ~RW[3], RegWrite);  // AND_Gate
  and and_2 (and_2_out, RW[3], RegWrite);
  RegisterFile_8R_NZ registerfile_8r_nz_1 (
    .RA(demultiplexer_3_out0), .RB(demultiplexer_2_out0), .RW(demultiplexer_1_out0), .CLK(CLK),
    .RegWrite(and_1_out), .BusW(BusW), .BusA(registerfile_8r_nz_1_busa), .BusB(registerfile_8r_nz_1_busb));
  RegisterFile_8R_NZ registerfile_8r_nz_2 (
    .RA(demultiplexer_3_out1), .RB(demultiplexer_2_out1), .RW(demultiplexer_1_out1), .CLK(CLK),
    .RegWrite(and_2_out), .BusW(BusW), .BusA(registerfile_8r_nz_2_busa), .BusB(registerfile_8r_nz_2_busb));
  Multiplexer #(.width(32), .enable("false")) multiplexer_1 (
    .in0(registerfile_8r_nz_1_busa), .in1(registerfile_8r_nz_2_busa), .out(BusA), .sel(RA[3]));
  Multiplexer #(.width(32), .enable("false")) multiplexer_2 (
    .in0(registerfile_8r_nz_1_busb), .in1(registerfile_8r_nz_2_busb), .out(BusB), .sel(RB[3]));
endmodule

module RegisterFile_32R (
  input  [4:0] RA,
  input  [4:0] RB,
  input  [4:0] RW,
  input  CLK,
  input  RegWrite,
  input  [31:0] BusW,
  output [31:0] BusA,
  output [31:0] BusB
);

  wire and_1_out, and_2_out;
  wire [3:0] demultiplexer_1_out0, demultiplexer_1_out1, demultiplexer_2_out0, demultiplexer_2_out1,
       demultiplexer_3_out0, demultiplexer_3_out1;
  wire [31:0] registerfile_16r_nz_1_busa, registerfile_16r_nz_1_busb, registerfile_16r_wz_1_busa,
       registerfile_16r_wz_1_busb;

  Demultiplexer #(.width(4), .enable("false")) demultiplexer_1 (
    .out0(demultiplexer_1_out0), .out1(demultiplexer_1_out1), .in(RW[3:0]), .sel(RW[4]));
  Demultiplexer #(.width(4), .enable("false")) demultiplexer_2 (
    .out0(demultiplexer_2_out0), .out1(demultiplexer_2_out1), .in(RB[3:0]), .sel(RB[4]));
  Demultiplexer #(.width(4), .enable("false")) demultiplexer_3 (
    .out0(demultiplexer_3_out0), .out1(demultiplexer_3_out1), .in(RA[3:0]), .sel(RA[4]));
  and and_1 (and_1_out, ~RW[4], RegWrite);  // AND_Gate
  and and_2 (and_2_out, RW[4], RegWrite);
  RegisterFile_16R_WZ registerfile_16r_wz_1 (
    .RA(demultiplexer_3_out0), .RB(demultiplexer_2_out0), .RW(demultiplexer_1_out0), .CLK(CLK),
    .RegWrite(and_1_out), .BusW(BusW), .BusA(registerfile_16r_wz_1_busa), .BusB(registerfile_16r_wz_1_busb));
  RegisterFile_16R_NZ registerfile_16r_nz_1 (
    .RA(demultiplexer_3_out1), .RB(demultiplexer_2_out1), .RW(demultiplexer_1_out1), .CLK(CLK),
    .RegWrite(and_2_out), .BusW(BusW), .BusA(registerfile_16r_nz_1_busa), .BusB(registerfile_16r_nz_1_busb));
  Multiplexer #(.width(32), .enable("false")) multiplexer_1 (
    .in0(registerfile_16r_wz_1_busa), .in1(registerfile_16r_nz_1_busa), .out(BusA), .sel(RA[4]));
  Multiplexer #(.width(32), .enable("false")) multiplexer_2 (
    .in0(registerfile_16r_wz_1_busb), .in1(registerfile_16r_nz_1_busb), .out(BusB), .sel(RB[4]));
endmodule
