// Logisim project v11_1.circ as structural Verilog
module RS_Latch (
  input  Reset,
  input  Set,
  output Output,
  output Negated_Output
);

  nor nor_1 (Output, Reset, Negated_Output);
  nor nor_2 (Negated_Output, Output, Set);
endmodule

module D_Latch (
  input  Clock,
  input  Data,
  output Output,
  output out_4
);

  wire and_1_out, and_2_out, not_1_out;

  not not_1 (not_1_out, Data);
  and and_1 (and_1_out, Clock, not_1_out);
  and and_2 (and_2_out, Clock, Data);
  RS_Latch rs_latch_1 (.Negated_Output(out_4), .Output(Output), .Reset(and_1_out), .Set(and_2_out));

  // Notes on the sheet:
  //   Negated Output
endmodule

module D_FlipFlop (
  input  Data,
  input  Clock,
  input  Write_Enable,
  output Output,
  output out_5
);

  wire d_latch_1_output, multiplexer_1_out, not_1_out;

  Multiplexer #(.enable("false")) multiplexer_1 (.in0(Output), .in1(Data), .out(multiplexer_1_out), .sel(Write_Enable));
  not not_1 (not_1_out, Clock);
  D_Latch d_latch_1 (.Output(d_latch_1_output), .Clock(Clock), .Data(multiplexer_1_out));  // open: out_4
  D_Latch d_latch_2 (.out_4(out_5), .Output(Output), .Clock(not_1_out), .Data(d_latch_1_output));

  // Notes on the sheet:
  //   Negated Output
endmodule

module Register_8bit (
  input  [7:0] Input,
  input  Clock,
  input  Write_Enable,
  output [7:0] Output
);

  D_FlipFlop d_flipflop_1 (
    .Output(Output[0]), .Clock(Clock), .Data(Input[0]), .Write_Enable(Write_Enable));  // open: out_5
  D_FlipFlop d_flipflop_2 (
    .Output(Output[1]), .Clock(Clock), .Data(Input[1]), .Write_Enable(Write_Enable));  // open: out_5
  D_FlipFlop d_flipflop_3 (
    .Output(Output[2]), .Clock(Clock), .Data(Input[2]), .Write_Enable(Write_Enable));  // open: out_5
  D_FlipFlop d_flipflop_4 (
    .Output(Output[3]), .Clock(Clock), .Data(Input[3]), .Write_Enable(Write_Enable));  // open: out_5
  D_FlipFlop d_flipflop_5 (
    .Output(Output[4]), .Clock(Clock), .Data(Input[4]), .Write_Enable(Write_Enable));  // open: out_5
  D_FlipFlop d_flipflop_6 (
    .Output(Output[5]), .Clock(Clock), .Data(Input[5]), .Write_Enable(Write_Enable));  // open: out_5
  D_FlipFlop d_flipflop_7 (
    .Output(Output[6]), .Clock(Clock), .Data(Input[6]), .Write_Enable(Write_Enable));  // open: out_5
  D_FlipFlop d_flipflop_8 (
    .Output(Output[7]), .Clock(Clock), .Data(Input[7]), .Write_Enable(Write_Enable));  // open: out_5
endmodule

module Register_File_8R_8b (
  input  [2:0] Register_A,
  input  [2:0] Register_B,
  input  [2:0] Register_Write,
  input  Clock,
  input  Write_Enable,
  input  [7:0] in_6,
  output [7:0] out_7,
  output [7:0] out_8
);

  wire and_1_out, and_2_out, and_3_out, and_4_out, and_5_out, and_6_out, and_7_out, decoder_1_out1,
       decoder_1_out2, decoder_1_out3, decoder_1_out4, decoder_1_out5, decoder_1_out6, decoder_1_out7,
       decoder_2_out0, decoder_2_out1, decoder_2_out2, decoder_2_out3, decoder_2_out4, decoder_2_out5,
       decoder_2_out6, decoder_2_out7, decoder_3_out0, decoder_3_out1, decoder_3_out2, decoder_3_out3,
       decoder_3_out4, decoder_3_out5, decoder_3_out6, decoder_3_out7;
  wire [7:0] register_8bit_1_output, register_8bit_2_output, register_8bit_3_output, register_8bit_4_output,
       register_8bit_5_output, register_8bit_6_output, register_8bit_7_output;

  Decoder #(.select(3), .enable("false")) decoder_1 (
    .out1(decoder_1_out1), .out2(decoder_1_out2), .out3(decoder_1_out3), .out4(decoder_1_out4),
    .out5(decoder_1_out5), .out6(decoder_1_out6), .out7(decoder_1_out7), .sel(Register_Write));  // open: out0
  and and_1 (and_1_out, decoder_1_out1, Write_Enable);
  and and_2 (and_2_out, decoder_1_out2, Write_Enable);
  and and_3 (and_3_out, decoder_1_out3, Write_Enable);
  and and_4 (and_4_out, decoder_1_out4, Write_Enable);
  and and_5 (and_5_out, decoder_1_out5, Write_Enable);
  and and_6 (and_6_out, decoder_1_out6, Write_Enable);
  and and_7 (and_7_out, decoder_1_out7, Write_Enable);
  Decoder #(.select(3), .enable("false")) decoder_2 (
    .out0(decoder_2_out0), .out1(decoder_2_out1), .out2(decoder_2_out2), .out3(decoder_2_out3),
    .out4(decoder_2_out4), .out5(decoder_2_out5), .out6(decoder_2_out6), .out7(decoder_2_out7),
    .sel(Register_A));
  Register_8bit register_8bit_1 (
    .Write_Enable(and_1_out), .Clock(Clock), .Input(in_6), .Output(register_8bit_1_output));
  Register_8bit register_8bit_2 (
    .Write_Enable(and_2_out), .Clock(Clock), .Input(in_6), .Output(register_8bit_2_output));
  Register_8bit register_8bit_3 (
    .Write_Enable(and_3_out), .Clock(Clock), .Input(in_6), .Output(register_8bit_3_output));
  Register_8bit register_8bit_4 (
    .Write_Enable(and_4_out), .Clock(Clock), .Input(in_6), .Output(register_8bit_4_output));
  Register_8bit register_8bit_5 (
    .Write_Enable(and_5_out), .Clock(Clock), .Input(in_6), .Output(register_8bit_5_output));
  Register_8bit register_8bit_6 (
    .Write_Enable(and_6_out), .Clock(Clock), .Input(in_6), .Output(register_8bit_6_output));
  Register_8bit register_8bit_7 (
    .Write_Enable(and_7_out), .Clock(Clock), .Input(in_6), .Output(register_8bit_7_output));
  assign out_7 = decoder_2_out0 ? {8{1'b0}} : 8'bz;  // Controlled_Buffer controlled_buffer_1
  assign out_7 = decoder_2_out1 ? register_8bit_1_output : 8'bz;  // Controlled_Buffer controlled_buffer_2
  assign out_7 = decoder_2_out2 ? register_8bit_2_output : 8'bz;  // Controlled_Buffer controlled_buffer_3
  assign out_7 = decoder_2_out3 ? register_8bit_3_output : 8'bz;  // Controlled_Buffer controlled_buffer_4
  assign out_7 = decoder_2_out4 ? register_8bit_4_output : 8'bz;  // Controlled_Buffer controlled_buffer_5
  assign out_7 = decoder_2_out5 ? register_8bit_5_output : 8'bz;  // Controlled_Buffer controlled_buffer_6
  assign out_7 = decoder_2_out6 ? register_8bit_6_output : 8'bz;  // Controlled_Buffer controlled_buffer_7
  assign out_7 = decoder_2_out7 ? register_8bit_7_output : 8'bz;  // Controlled_Buffer controlled_buffer_8
  Decoder #(.select(3), .enable("false")) decoder_3 (
    .out0(decoder_3_out0), .out1(decoder_3_out1), .out2(decoder_3_out2), .out3(decoder_3_out3),
    .out4(decoder_3_out4), .out5(decoder_3_out5), .out6(decoder_3_out6), .out7(decoder_3_out7),
    .sel(Register_B));
  assign out_8 = decoder_3_out0 ? {8{1'b0}} : 8'bz;  // Controlled_Buffer controlled_buffer_9
  assign out_8 = decoder_3_out1 ? register_8bit_1_output : 8'bz;  // Controlled_Buffer controlled_buffer_10
  assign out_8 = decoder_3_out2 ? register_8bit_2_output : 8'bz;  // Controlled_Buffer controlled_buffer_11
  assign out_8 = decoder_3_out3 ? register_8bit_3_output : 8'bz;  // Controlled_Buffer controlled_buffer_12
  assign out_8 = decoder_3_out4 ? register_8bit_4_output : 8'bz;  // Controlled_Buffer controlled_buffer_13
  assign out_8 = decoder_3_out5 ? register_8bit_5_output : 8'bz;  // Controlled_Buffer controlled_buffer_14
  assign out_8 = decoder_3_out6 ? register_8bit_6_output : 8'bz;  // Controlled_Buffer controlled_buffer_15
  assign out_8 = decoder_3_out7 ? register_8bit_7_output : 8'bz;  // Controlled_Buffer controlled_buffer_16

  // Notes on the sheet:
  //   Bus Write
  //   Bus A
  //   Bus B
endmodule

module Adder_1b (
  input  A,
  input  B,
  input  Cin,
  output R,
  output Cout
);

  wire and_1_out, and_2_out, and_3_out, and_4_out, and_5_out, and_6_out, and_7_out, not_1_out, not_2_out,
       not_3_out, not_4_out, not_5_out, not_6_out;

  not not_1 (not_1_out, A);
  not not_2 (not_2_out, B);
  not not_3 (not_3_out, A);
  not not_4 (not_4_out, Cin);
  not not_5 (not_5_out, B);
  not not_6 (not_6_out, Cin);
  and and_1 (and_1_out, not_1_out, not_2_out, Cin);
  and and_2 (and_2_out, not_3_out, B, not_4_out);
  and and_3 (and_3_out, A, not_5_out, not_6_out);
  and and_4 (and_4_out, A, B, Cin);
  and and_5 (and_5_out, B, Cin);
  and and_6 (and_6_out, A, Cin);
  or or_1 (Cout, and_5_out, and_6_out, and_7_out);
  and and_7 (and_7_out, A, B);
  or or_2 (R, and_1_out, and_2_out, and_3_out, and_4_out);
endmodule

module Adder_2b (
  input  [1:0] A,
  input  [1:0] B,
  input  Cin,
  output [1:0] R,
  output Cout
);

  wire adder_1b_2_cout;

  Adder_1b adder_1b_1 (.A(A[1]), .B(B[1]), .Cin(adder_1b_2_cout), .R(R[1]), .Cout(Cout));
  Adder_1b adder_1b_2 (.A(A[0]), .B(B[0]), .Cin(Cin), .R(R[0]), .Cout(adder_1b_2_cout));
endmodule

module Adder_4b (
  input  [3:0] A,
  input  [3:0] B,
  input  Cin,
  output [3:0] R,
  output Cout
);

  wire adder_2b_2_cout;

  Adder_2b adder_2b_1 (.A(A[3:2]), .B(B[3:2]), .Cin(adder_2b_2_cout), .R(R[3:2]), .Cout(Cout));
  Adder_2b adder_2b_2 (.A(A[1:0]), .B(B[1:0]), .Cin(Cin), .R(R[1:0]), .Cout(adder_2b_2_cout));
endmodule

module ALU (
  input  [3:0] A,
  input  [3:0] B,
  input  [3:0] Ctrl,
  output [3:0] R
);

  wire adder_4b_1_cout;
  wire [1:0] alu_ctrl_1_sl;
  wire [3:0] adder_4b_1_r, and_1_out, or_1_out, xor_1_out, xor_2_out;
  wire [3:3] alu_ctrl_1_as;

  ALU_Ctrl alu_ctrl_1 (.Ctrl(Ctrl), .AS(alu_ctrl_1_as[3]), .SL(alu_ctrl_1_sl));
  assign xor_1_out = B ^ {4{alu_ctrl_1_as[3]}};  // XOR_Gate xor_1, 4 bits wide
  assign and_1_out = A & B;  // AND_Gate and_1, 4 bits wide
  assign or_1_out = A | B;  // OR_Gate or_1, 4 bits wide
  assign xor_2_out = A ^ B;  // XOR_Gate xor_2, 4 bits wide
  Adder_4b adder_4b_1 (.A(A), .B(xor_1_out), .Cin(alu_ctrl_1_as[3]), .R(adder_4b_1_r), .Cout(adder_4b_1_cout));
  Multiplexer #(.select(2), .width(4), .enable("false")) multiplexer_1 (
    .in0(adder_4b_1_r), .in1(and_1_out), .in2(or_1_out), .in3(xor_2_out), .out(R), .sel(alu_ctrl_1_sl));
  // also tied to GND on the sheet: adder_4b_1_cout
endmodule

module ALU_Ctrl (
  input  [3:0] Ctrl,
  output AS,
  output [1:0] SL
);

  wire and_1_out, and_2_out, not_1_out;

  not not_1 (not_1_out, Ctrl[1]);
  not not_2 (SL[0], Ctrl[1]);
  and and_1 (and_1_out, Ctrl[2], not_1_out);
  and and_2 (and_2_out, Ctrl[3], Ctrl[1]);
  or or_1 (SL[1], and_1_out, and_2_out);

  assign AS = Ctrl[2];
endmodule
