// Logisim project v11_2.circ as structural Verilog
module PC (
  input  R,
  output [31:0] out_2
);

  wire clock_1_out;
  wire [29:0] incrementer_1_p3;
  wire [31:0] PC_q;

  Clock clock_1 (.out(clock_1_out));
  Register #(.width(32), .trigger("falling")) PC (
    .D({incrementer_1_p3, 2'b00}), .en(1'b1), .clk(clock_1_out), .Q(PC_q), .clr(R));
  // Incrementer #(.width(30)) incrementer_1: pin names not known; wires that end beside it: PC_q, PC_q[31:2], incrementer_1_p3
  // MIPSProgramROM mipsprogramrom_1: pin names not known; wires that end beside it: out_2
  // RegisterFile #(.trigger("falling")) registerfile_1: pin names not known
  // Mips_ALU mips_alu_1: pin names not known
  // MIPS_RAM #(.addrWidth(24)) mips_ram_1: pin names not known
  Multiplexer #(.enable("false")) multiplexer_1 ();  // open: in0, in1, out, sel

  // Notes on the sheet:
  //   contents of mipsprogramrom_1 (hex, n*v repeats v):
  //   addiu $t1, $0, 0xA or $t2, $t0, $t1 sll $t3, $t2, 3 sw $t3, 0($0) lw $t4, 0($0)
endmodule
