// Logisim project v12.circ as structural Verilog
module CPU (
  input  R,
  input  RAM_CLR,
  output [31:0] out_3
);

  wire clock_1_out, main_ctrl_1_load, main_ctrl_1_mem_to_reg, main_ctrl_1_regwrite, main_ctrl_1_store,
       or_1_out, registerfile_1_p7;
  wire [3:0] funct_to_alu_1_alu_ctrl, mips_alu_1_p3, opcode_to_alu_1_alu_ctrl;
  wire [4:0] registerfile_1_p4;
  wire [29:0] incrementer_1_p3;
  wire [31:0] bit_extender_1_out, mips_alu_1_p5, mips_ram_1_p7, multiplexer_1_out, multiplexer_3_out, PC_q,
       registerfile_1_p8;

  Clock clock_1 (.out(clock_1_out));
  Register #(.width(32), .trigger("falling")) PC (
    .D({incrementer_1_p3, 2'b00}), .en(1'b1), .clk(clock_1_out), .Q(PC_q), .clr(R));
  // Incrementer #(.width(30)) incrementer_1: pin names not known; wires that end beside it: PC_q, PC_q[31:2], incrementer_1_p3
  // MIPSProgramROM mipsprogramrom_1: pin names not known; wires that end beside it: out_3
  // Probe on out_3[31:26]
  // Probe on out_3[25:21]
  // Probe on out_3[20:16]
  // Probe on out_3[15:11]
  // Probe on out_3[10:6]
  // Probe on out_3[5:0]
  // Probe on out_3[31:26]
  // Probe on out_3[25:21]
  // Probe on out_3[20:16]
  // Probe on out_3[15:0]
  Main_CTRL main_ctrl_1 (
    .OPCODE(out_3[31:26]), .RegWrite(main_ctrl_1_regwrite), .Load(main_ctrl_1_load),
    .Store(main_ctrl_1_store), .MEM_TO_REG(main_ctrl_1_mem_to_reg));
  Multiplexer #(.width(32), .enable("false")) multiplexer_1 (
    .in0(mips_alu_1_p5), .in1(mips_ram_1_p7), .out(multiplexer_1_out), .sel(main_ctrl_1_mem_to_reg));
  // RegisterFile #(.trigger("falling")) registerfile_1: pin names not known; wires that end beside it: multiplexer_1_out, clock_1_out, main_ctrl_1_regwrite, registerfile_1_p4, out_3[25:21], out_3[20:16], registerfile_1_p7, registerfile_1_p8
  or or_1 (or_1_out, out_3[26], out_3[27], out_3[28], out_3[29], out_3[30], out_3[31]);
  Multiplexer #(.width(5), .enable("false")) multiplexer_2 (
    .in0(out_3[15:11]), .in1(out_3[20:16]), .out(registerfile_1_p4), .sel(or_1_out));
  assign bit_extender_1_out = {{16{out_3[15]}}, out_3[15:0]};  // Bit_Extender bit_extender_1
  Multiplexer #(.width(32), .enable("false")) multiplexer_3 (
    .in0(registerfile_1_p8), .in1(bit_extender_1_out), .out(multiplexer_3_out), .sel(or_1_out));
  // Mips_ALU mips_alu_1: pin names not known; wires that end beside it: registerfile_1_p7, multiplexer_3_out, mips_alu_1_p3, out_3[10:6], mips_alu_1_p5
  FUNCT_to_ALU funct_to_alu_1 (.FUNCT(out_3[5:0]), .ALU_CTRL(funct_to_alu_1_alu_ctrl));
  OPCODE_to_ALU opcode_to_alu_1 (.OPCODE(out_3[31:26]), .ALU_CTRL(opcode_to_alu_1_alu_ctrl));
  Multiplexer #(.width(4), .enable("false")) multiplexer_4 (
    .in0(funct_to_alu_1_alu_ctrl), .in1(opcode_to_alu_1_alu_ctrl), .out(mips_alu_1_p3), .sel(or_1_out));
  // MIPS_RAM #(.addrWidth(24)) mips_ram_1: pin names not known; wires that end beside it: mips_alu_1_p5[23:0], registerfile_1_p8, main_ctrl_1_store, clock_1_out, main_ctrl_1_load, RAM_CLR, mips_ram_1_p7

  // Notes on the sheet:
  //   contents of mipsprogramrom_1 (hex, n*v repeats v):
  //   addiu $t1, $0, 0xA or $t2, $t0, $t1 sll $t3, $t2, 3 sw $t3, 0($0) lw $t4, 0($0)
endmodule

module Main_CTRL (
  input  [5:0] OPCODE,
  output RegWrite,
  output Load,
  output Store,
  output MEM_TO_REG
);

  wire not_1_out, not_2_out, not_3_out, not_4_out;

  not not_1 (not_1_out, OPCODE[3]);
  not not_2 (not_2_out, OPCODE[1]);
  not not_3 (not_3_out, OPCODE[3]);
  and and_1 (Store, OPCODE[5], OPCODE[3]);
  not not_4 (not_4_out, OPCODE[3]);
  or or_1 (RegWrite, not_1_out, not_2_out);
  and and_2 (Load, not_3_out, OPCODE[1]);
  and and_3 (MEM_TO_REG, not_4_out, OPCODE[1]);
endmodule

module OPCODE_to_ALU (
  input  [5:0] OPCODE,
  output [3:0] ALU_CTRL
);


  assign ALU_CTRL = 4'b0010;
endmodule

module FUNCT_to_ALU (
  input  [5:0] FUNCT,
  output [3:0] ALU_CTRL
);


  assign ALU_CTRL = {FUNCT[2], 1'b0, FUNCT[0], 1'b0};
endmodule
