// Logisim project v7.circ as structural Verilog
module RS_Latch (
  input  Reset,
  input  Set,
  output Output,
  output Negated_Output
);

  nor nor_1 (Output, Reset, Negated_Output);
  nor nor_2 (Negated_Output, Output, Set);
endmodule

module D_Latch (
  input  Clock,
  input  Data,
  output Output,
  output out_4
);

  wire and_1_out, and_2_out, not_1_out;

  not not_1 (not_1_out, Data);
  and and_1 (and_1_out, Clock, not_1_out);
  and and_2 (and_2_out, Clock, Data);
  RS_Latch rs_latch_1 (.Set(and_2_out), .Negated_Output(out_4), .Reset(and_1_out), .Output(Output));

  // Notes on the sheet:
  //   Negated Output
endmodule

module D_FlipFlop (
  input  Data,
  input  Clock,
  input  Write_Enable,
  output Output,
  output out_5
);

  wire d_latch_1_output, multiplexer_1_out, not_1_out;

  Multiplexer #(.enable("false")) multiplexer_1 (.in0(Output), .in1(Data), .out(multiplexer_1_out), .sel(Write_Enable));
  not not_1 (not_1_out, Clock);
  D_Latch d_latch_1 (.Data(multiplexer_1_out), .Clock(Clock), .Output(d_latch_1_output));  // open: out_4
  D_Latch d_latch_2 (.Data(d_latch_1_output), .out_4(out_5), .Clock(not_1_out), .Output(Output));

  // Notes on the sheet:
  //   Negated Output
endmodule

module Register_8bit (
  input  [7:0] Input,
  input  Clock,
  input  Write_Enable,
  output [7:0] Output
);

  D_FlipFlop d_flipflop_1 (
    .Output(Output[0]), .Data(Input[0]), .Clock(Clock), .Write_Enable(Write_Enable));  // open: out_5
  D_FlipFlop d_flipflop_2 (
    .Output(Output[1]), .Data(Input[1]), .Clock(Clock), .Write_Enable(Write_Enable));  // open: out_5
  D_FlipFlop d_flipflop_3 (
    .Output(Output[2]), .Data(Input[2]), .Clock(Clock), .Write_Enable(Write_Enable));  // open: out_5
  D_FlipFlop d_flipflop_4 (
    .Output(Output[3]), .Data(Input[3]), .Clock(Clock), .Write_Enable(Write_Enable));  // open: out_5
  D_FlipFlop d_flipflop_5 (
    .Output(Output[4]), .Data(Input[4]), .Clock(Clock), .Write_Enable(Write_Enable));  // open: out_5
  D_FlipFlop d_flipflop_6 (
    .Output(Output[5]), .Data(Input[5]), .Clock(Clock), .Write_Enable(Write_Enable));  // open: out_5
  D_FlipFlop d_flipflop_7 (
    .Output(Output[6]), .Data(Input[6]), .Clock(Clock), .Write_Enable(Write_Enable));  // open: out_5
  D_FlipFlop d_flipflop_8 (
    .Output(Output[7]), .Data(Input[7]), .Clock(Clock), .Write_Enable(Write_Enable));  // open: out_5
endmodule

module Register_File_8R_8b (
  input  [2:0] Register_A,
  input  [2:0] Register_B,
  input  [2:0] Register_Write,
  input  Clock,
  input  Write_Enable,
  input  [7:0] in_6,
  output [7:0] out_7,
  output [7:0] out_8
);

  wire and_1_out, and_2_out, and_3_out, and_4_out, and_5_out, and_6_out, and_7_out, decoder_1_out1,
       decoder_1_out2, decoder_1_out3, decoder_1_out4, decoder_1_out5, decoder_1_out6, decoder_1_out7,
       decoder_2_out0, decoder_2_out1, decoder_2_out2, decoder_2_out3, decoder_2_out4, decoder_2_out5,
       decoder_2_out6, decoder_2_out7, decoder_3_out0, decoder_3_out1, decoder_3_out2, decoder_3_out3,
       decoder_3_out4, decoder_3_out5, decoder_3_out6, decoder_3_out7;
  wire [7:0] register_8bit_1_output, register_8bit_2_output, register_8bit_3_output, register_8bit_4_output,
       register_8bit_5_output, register_8bit_6_output, register_8bit_7_output;

  Decoder #(.select(3), .enable("false")) decoder_1 (
    .out1(decoder_1_out1), .out2(decoder_1_out2), .out3(decoder_1_out3), .out4(decoder_1_out4),
    .out5(decoder_1_out5), .out6(decoder_1_out6), .out7(decoder_1_out7), .sel(Register_Write));  // open: out0
  and and_1 (and_1_out, decoder_1_out1, Write_Enable);
  and and_2 (and_2_out, decoder_1_out2, Write_Enable);
  and and_3 (and_3_out, decoder_1_out3, Write_Enable);
  and and_4 (and_4_out, decoder_1_out4, Write_Enable);
  and and_5 (and_5_out, decoder_1_out5, Write_Enable);
  and and_6 (and_6_out, decoder_1_out6, Write_Enable);
  and and_7 (and_7_out, decoder_1_out7, Write_Enable);
  Decoder #(.select(3), .enable("false")) decoder_2 (
    .out0(decoder_2_out0), .out1(decoder_2_out1), .out2(decoder_2_out2), .out3(decoder_2_out3),
    .out4(decoder_2_out4), .out5(decoder_2_out5), .out6(decoder_2_out6), .out7(decoder_2_out7),
    .sel(Register_A));
  Register_8bit register_8bit_1 (
    .Output(register_8bit_1_output), .Write_Enable(and_1_out), .Input(in_6), .Clock(Clock));
  Register_8bit register_8bit_2 (
    .Output(register_8bit_2_output), .Write_Enable(and_2_out), .Input(in_6), .Clock(Clock));
  Register_8bit register_8bit_3 (
    .Output(register_8bit_3_output), .Write_Enable(and_3_out), .Input(in_6), .Clock(Clock));
  Register_8bit register_8bit_4 (
    .Output(register_8bit_4_output), .Write_Enable(and_4_out), .Input(in_6), .Clock(Clock));
  Register_8bit register_8bit_5 (
    .Output(register_8bit_5_output), .Write_Enable(and_5_out), .Input(in_6), .Clock(Clock));
  Register_8bit register_8bit_6 (
    .Output(register_8bit_6_output), .Write_Enable(and_6_out), .Input(in_6), .Clock(Clock));
  Register_8bit register_8bit_7 (
    .Output(register_8bit_7_output), .Write_Enable(and_7_out), .Input(in_6), .Clock(Clock));
  assign out_7 = decoder_2_out0 ? {8{1'b0}} : 8'bz;  // Controlled_Buffer controlled_buffer_1
  assign out_7 = decoder_2_out1 ? register_8bit_1_output : 8'bz;  // Controlled_Buffer controlled_buffer_2
  assign out_7 = decoder_2_out2 ? register_8bit_2_output : 8'bz;  // Controlled_Buffer controlled_buffer_3
  assign out_7 = decoder_2_out3 ? register_8bit_3_output : 8'bz;  // Controlled_Buffer controlled_buffer_4
  assign out_7 = decoder_2_out4 ? register_8bit_4_output : 8'bz;  // Controlled_Buffer controlled_buffer_5
  assign out_7 = decoder_2_out5 ? register_8bit_5_output : 8'bz;  // Controlled_Buffer controlled_buffer_6
  assign out_7 = decoder_2_out6 ? register_8bit_6_output : 8'bz;  // Controlled_Buffer controlled_buffer_7
  assign out_7 = decoder_2_out7 ? register_8bit_7_output : 8'bz;  // Controlled_Buffer controlled_buffer_8
  Decoder #(.select(3), .enable("false")) decoder_3 (
    .out0(decoder_3_out0), .out1(decoder_3_out1), .out2(decoder_3_out2), .out3(decoder_3_out3),
    .out4(decoder_3_out4), .out5(decoder_3_out5), .out6(decoder_3_out6), .out7(decoder_3_out7),
    .sel(Register_B));
  assign out_8 = decoder_3_out0 ? {8{1'b0}} : 8'bz;  // Controlled_Buffer controlled_buffer_9
  assign out_8 = decoder_3_out1 ? register_8bit_1_output : 8'bz;  // Controlled_Buffer controlled_buffer_10
  assign out_8 = decoder_3_out2 ? register_8bit_2_output : 8'bz;  // Controlled_Buffer controlled_buffer_11
  assign out_8 = decoder_3_out3 ? register_8bit_3_output : 8'bz;  // Controlled_Buffer controlled_buffer_12
  assign out_8 = decoder_3_out4 ? register_8bit_4_output : 8'bz;  // Controlled_Buffer controlled_buffer_13
  assign out_8 = decoder_3_out5 ? register_8bit_5_output : 8'bz;  // Controlled_Buffer controlled_buffer_14
  assign out_8 = decoder_3_out6 ? register_8bit_6_output : 8'bz;  // Controlled_Buffer controlled_buffer_15
  assign out_8 = decoder_3_out7 ? register_8bit_7_output : 8'bz;  // Controlled_Buffer controlled_buffer_16

  // Notes on the sheet:
  //   Bus Write
  //   Bus A
  //   Bus B
endmodule
