// Logisim project mahir_suljic_22128.circ as structural Verilog
module CPU (
  input  RAM_CLEAR,
  input  PC_RESET
);

  wire alu_zero_1_zero, CLK_out, jr_handle_1_jr, main_ctrl_1_alusrc, main_ctrl_1_extop, main_ctrl_1_link,
       main_ctrl_1_memread, main_ctrl_1_memtoreg, main_ctrl_1_memwrite, main_ctrl_1_regwrite,
       next_pc_1_pc_src, r_type_test_1_r_type;
  wire [2:0] main_ctrl_1_jb_ctrl;
  wire [3:0] alu_ctrl_1_alu_ctrl;
  wire [4:0] multiplexer_2_out, multiplexer_3_out;
  wire [29:0] next_pc_1_address;
  wire [31:0] bit_extender_1_out_32b, mips_alu_1_p5, mips_ram_1_p7, mipsprogramrom_1_p2, multiplexer_1_out,
       multiplexer_4_out, multiplexer_5_out, pc_1_pc, registerfile_1_p7, registerfile_1_p8;
  wire [31:2] pc_1_pc_incr_30b;

  Clock CLK (.out(CLK_out));
  PC pc_1 (
    .JR(jr_handle_1_jr), .REG_BUS(registerfile_1_p7), .PC_SRC(next_pc_1_pc_src), .ADDR(next_pc_1_address),
    .PC_RESET(PC_RESET), .CLK(CLK_out), .PC_INCR_30b(pc_1_pc_incr_30b), .PC(pc_1_pc));
  // MIPSProgramROM mipsprogramrom_1: pin names not known; wires that end beside it: pc_1_pc, mipsprogramrom_1_p2
  // Probe on mipsprogramrom_1_p2[25:0]
  // Probe on mipsprogramrom_1_p2[31:26]
  // Probe on mipsprogramrom_1_p2[25:21]
  // Probe on mipsprogramrom_1_p2[20:16]
  // Probe on mipsprogramrom_1_p2[15:11]
  // Probe on mipsprogramrom_1_p2[10:6]
  // Probe on mipsprogramrom_1_p2[5:0]
  // Probe on mipsprogramrom_1_p2[15:0]
  R_TYPE_TEST r_type_test_1 (.OPCODE(mipsprogramrom_1_p2[31:26]), .R_TYPE(r_type_test_1_r_type));
  ALU_CTRL alu_ctrl_1 (
    .FUNCT(mipsprogramrom_1_p2[5:0]), .OPCODE(mipsprogramrom_1_p2[31:26]), .ALU_CTRL(alu_ctrl_1_alu_ctrl));
  MAIN_CTRL main_ctrl_1 (
    .OPCODE(mipsprogramrom_1_p2[31:26]), .RegWrite(main_ctrl_1_regwrite), .ExtOp(main_ctrl_1_extop),
    .MemRead(main_ctrl_1_memread), .MemWrite(main_ctrl_1_memwrite), .MemToReg(main_ctrl_1_memtoreg),
    .ALUSrc(main_ctrl_1_alusrc), .JB_CTRL(main_ctrl_1_jb_ctrl), .Link(main_ctrl_1_link));
  JR_HANDLE jr_handle_1 (.FUNCT(mipsprogramrom_1_p2[5:0]), .R_TYPE(r_type_test_1_r_type), .JR(jr_handle_1_jr));
  Multiplexer #(.width(32), .enable("false")) multiplexer_1 (
    .in0(multiplexer_5_out), .in1({pc_1_pc_incr_30b, 2'b00}), .out(multiplexer_1_out), .sel(main_ctrl_1_link));
  Multiplexer #(.width(5), .enable("false")) multiplexer_2 (
    .in0(mipsprogramrom_1_p2[20:16]), .in1(mipsprogramrom_1_p2[15:11]), .out(multiplexer_2_out),
    .sel(r_type_test_1_r_type));
  Multiplexer #(.width(5), .enable("false")) multiplexer_3 (
    .in0(multiplexer_2_out), .in1({5{1'b1}}), .out(multiplexer_3_out), .sel(main_ctrl_1_link));
  // RegisterFile #(.trigger("falling")) registerfile_1: pin names not known; wires that end beside it: multiplexer_1_out, CLK_out, main_ctrl_1_regwrite, multiplexer_3_out, mipsprogramrom_1_p2[25:21], mipsprogramrom_1_p2[20:16], registerfile_1_p7, registerfile_1_p8
  BIT_EXTENDER bit_extender_1 (
    .IN_16b(mipsprogramrom_1_p2[15:0]), .ExtOp(main_ctrl_1_extop), .OUT_32b(bit_extender_1_out_32b));
  Multiplexer #(.width(32), .enable("false")) multiplexer_4 (
    .in0(registerfile_1_p8), .in1(bit_extender_1_out_32b), .out(multiplexer_4_out), .sel(main_ctrl_1_alusrc));
  // Mips_ALU mips_alu_1: pin names not known; wires that end beside it: registerfile_1_p7, multiplexer_4_out, alu_ctrl_1_alu_ctrl, mipsprogramrom_1_p2[10:6], mips_alu_1_p5
  Multiplexer #(.width(32), .enable("false")) multiplexer_5 (
    .in0(mips_alu_1_p5), .in1(mips_ram_1_p7), .out(multiplexer_5_out), .sel(main_ctrl_1_memtoreg));
  ALU_Zero alu_zero_1 (.ALU_OUT(mips_alu_1_p5), .Zero(alu_zero_1_zero));
  // MIPS_RAM #(.addrWidth(24)) mips_ram_1: pin names not known; wires that end beside it: mips_alu_1_p5[23:0], registerfile_1_p8, main_ctrl_1_memwrite, CLK_out, main_ctrl_1_memread, RAM_CLEAR, mips_ram_1_p7
  NEXT_PC next_pc_1 (
    .PC(pc_1_pc_incr_30b), .ADDR(mipsprogramrom_1_p2[25:0]), .JB_CTRL(main_ctrl_1_jb_ctrl),
    .Zero(alu_zero_1_zero), .Address(next_pc_1_address), .PC_Src(next_pc_1_pc_src));

  // Notes on the sheet:
  //   contents of mipsprogramrom_1 (hex, n*v repeats v):
  //   funkcija: subu $2, $4, $5 jr $31  main: addiu $8, $0, 4 ori $9, $0, 0xabcd sll $9, $9, 16 ori $9,
  //   $9, 0x1234 sw $9, 0($8) sw $9, 4($8) ori $10, $0, 4 addu $12, $8, $10 lw $13, 0($12) addu $5, $0,
  //   $13 bne   $5, $0, razlicito addiu $4, $5, -8 j     krajif razlicito: addiu $4, $5, 8 krajif:  jal
  //   funkcija sw $2, 8($8)  # Nakon izvrsenja programa u RAM memoriji bi trebalo da budu podaci: # adresa
  //   0: 0xabcd1234 # adresa 4: 0xabcd1234 # adresa 8: 0x00000008 # Ako je na adresi 8 vrijednost
  //   0xfffffff8 onda branch ne radi kako bi trebalo
endmodule

module PC (
  input  JR,
  input  [31:0] REG_BUS,
  input  PC_SRC,
  input  [29:0] ADDR,
  input  PC_RESET,
  input  CLK,
  output [29:0] PC_INCR_30b,
  output [31:0] PC
);

  wire not_1_out;
  wire [29:0] multiplexer_1_out, multiplexer_2_out;

  not not_1 (not_1_out, JR);
  Multiplexer #(.width(30), .enable("false")) multiplexer_1 (
    .in0(REG_BUS[31:2]), .in1(multiplexer_2_out), .out(multiplexer_1_out), .sel(not_1_out));
  Multiplexer #(.width(30), .enable("false")) multiplexer_2 (
    .in0(PC_INCR_30b), .in1(ADDR), .out(multiplexer_2_out), .sel(PC_SRC));
  Register #(.width(32), .trigger("falling")) register_1 (
    .D({multiplexer_1_out, 2'b00}), .en(1'b1), .clk(CLK), .Q(PC), .clr(PC_RESET));
  // Incrementer #(.width(30)) incrementer_1: pin names not known; wires that end beside it: PC[31:2], PC_INCR_30b
endmodule

module MAIN_CTRL (
  input  [5:0] OPCODE,
  output RegWrite,
  output ExtOp,
  output MemRead,
  output MemWrite,
  output MemToReg,
  output ALUSrc,
  output [2:0] JB_CTRL,
  output Link
);

  wire and_2_out, and_3_out, and_4_out, and_5_out, not_1_out, not_2_out, not_3_out, not_4_out, not_5_out,
       not_6_out, not_7_out, not_8_out, not_9_out, not_10_out, not_11_out, not_12_out, not_13_out;

  not not_1 (not_1_out, OPCODE[2]);
  not not_2 (not_2_out, OPCODE[1]);
  not not_3 (not_3_out, OPCODE[3]);
  not not_4 (not_4_out, OPCODE[2]);
  not not_5 (not_5_out, OPCODE[5]);
  not not_6 (not_6_out, OPCODE[3]);
  and and_1 (MemWrite, OPCODE[5], OPCODE[3]);
  or or_1 (ALUSrc, OPCODE[1], OPCODE[3]);
  not not_7 (not_7_out, OPCODE[5]);
  not not_8 (not_8_out, OPCODE[3]);
  not not_9 (not_9_out, OPCODE[3]);
  not not_10 (not_10_out, OPCODE[0]);
  not not_11 (not_11_out, OPCODE[3]);
  not not_12 (not_12_out, OPCODE[1]);
  not not_13 (not_13_out, OPCODE[5]);
  and and_2 (and_2_out, not_1_out, not_2_out);
  and and_3 (and_3_out, not_3_out, not_4_out, OPCODE[0]);
  and and_4 (and_4_out, not_5_out, OPCODE[3]);
  and and_5 (and_5_out, not_6_out, OPCODE[2]);
  and and_6 (JB_CTRL[2], not_7_out, not_8_out, OPCODE[1]);
  and and_7 (JB_CTRL[1], not_9_out, OPCODE[2], not_10_out);
  and and_8 (JB_CTRL[0], not_11_out, not_12_out, OPCODE[0]);
  and and_9 (Link, not_13_out, OPCODE[1], OPCODE[0]);
  or or_2 (RegWrite, and_2_out, and_3_out, and_4_out);
  or or_3 (ExtOp, and_5_out, OPCODE[5]);

  assign MemRead = OPCODE[5];
  assign MemToReg = OPCODE[5];

  // Notes on the sheet:
  //   2 - j
  //   1 - beq
  //   0 - bne
endmodule

module ALU_CTRL (
  input  [5:0] FUNCT,
  input  [5:0] OPCODE,
  output [3:0] ALU_CTRL
);

  wire or_1_out;
  wire [3:0] ij_type_alu_ctrl_1_alu_ctrl, r_type_alu_ctrl_1_alu_ctrl;

  or or_1 (or_1_out, OPCODE[0], OPCODE[1], OPCODE[2], OPCODE[3], OPCODE[4], OPCODE[5]);
  R_TYPE_ALU_CTRL r_type_alu_ctrl_1 (.FUNCT(FUNCT), .ALU_CTRL(r_type_alu_ctrl_1_alu_ctrl));
  IJ_TYPE_ALU_CTRL ij_type_alu_ctrl_1 (.OPCODE(OPCODE), .ALU_CTRL(ij_type_alu_ctrl_1_alu_ctrl));
  Multiplexer #(.width(4), .enable("false")) multiplexer_1 (
    .in0(r_type_alu_ctrl_1_alu_ctrl), .in1(ij_type_alu_ctrl_1_alu_ctrl), .out(ALU_CTRL), .sel(or_1_out));
endmodule

module R_TYPE_ALU_CTRL (
  input  [5:0] FUNCT,
  output [3:0] ALU_CTRL
);

  wire not_1_out;

  and and_1 (ALU_CTRL[1], FUNCT[5], FUNCT[0]);
  not not_1 (not_1_out, FUNCT[5]);
  and and_2 (ALU_CTRL[0], not_1_out, FUNCT[0]);

  assign ALU_CTRL[3:2] = FUNCT[2:1];
endmodule

module IJ_TYPE_ALU_CTRL (
  input  [5:0] OPCODE,
  output [3:0] ALU_CTRL
);

  wire and_2_out, and_3_out, not_1_out, not_2_out, not_3_out, not_4_out;

  and and_1 (ALU_CTRL[3], OPCODE[3], OPCODE[2]);
  not not_1 (not_1_out, OPCODE[3]);
  not not_2 (not_2_out, OPCODE[1]);
  not not_3 (not_3_out, OPCODE[0]);
  not not_4 (not_4_out, OPCODE[3]);
  and and_2 (and_2_out, not_1_out, not_2_out);
  and and_3 (and_3_out, OPCODE[1], not_3_out);
  or or_1 (ALU_CTRL[1], not_4_out, OPCODE[0]);
  or or_2 (ALU_CTRL[2], and_2_out, and_3_out);

  assign ALU_CTRL[0] = 1'b0;
endmodule

module NEXT_PC (
  input  [29:0] PC,
  input  [25:0] ADDR,
  input  [2:0] JB_CTRL,
  input  Zero,
  output [29:0] Address,
  output PC_Src
);

  wire and_1_out, and_2_out;
  wire [29:0] adder_1_out, bit_extender_1_out;

  assign bit_extender_1_out = {{14{1'b0}}, ADDR[15:0]};  // Bit_Extender bit_extender_1
  Adder #(.width(30)) adder_1 (.a(PC), .b(bit_extender_1_out), .out(adder_1_out));  // open: cin, cout
  Multiplexer #(.width(30), .enable("false")) multiplexer_1 (
    .in0(adder_1_out), .in1({PC[29:26], ADDR}), .out(Address), .sel(JB_CTRL[2]));
  or or_1 (PC_Src, and_1_out, JB_CTRL[2], and_2_out);
  and and_1 (and_1_out, Zero, JB_CTRL[1]);
  and and_2 (and_2_out, ~Zero, JB_CTRL[0]);  // AND_Gate

  // Notes on the sheet:
  //   2 - j
  //   0 - bne
  //   1 - beq
endmodule

module ALU_Zero (
  input  [31:0] ALU_OUT,
  output Zero
);

  nor nor_1 (Zero, ALU_OUT[0], ALU_OUT[1], ALU_OUT[2], ALU_OUT[3], ALU_OUT[4], ALU_OUT[5], ALU_OUT[6], ALU_OUT[7], ALU_OUT[8], ALU_OUT[9], ALU_OUT[10], ALU_OUT[11], ALU_OUT[12], ALU_OUT[13], ALU_OUT[14], ALU_OUT[15], ALU_OUT[16], ALU_OUT[17], ALU_OUT[18], ALU_OUT[19], ALU_OUT[20], ALU_OUT[21], ALU_OUT[22], ALU_OUT[23], ALU_OUT[24], ALU_OUT[25], ALU_OUT[26], ALU_OUT[27], ALU_OUT[28], ALU_OUT[29], ALU_OUT[30], ALU_OUT[31]);
endmodule

module R_TYPE_TEST (
  input  [5:0] OPCODE,
  output R_TYPE
);

  nor nor_1 (R_TYPE, OPCODE[0], OPCODE[1], OPCODE[2], OPCODE[3], OPCODE[4], OPCODE[5]);
endmodule

module JR_HANDLE (
  input  [5:0] FUNCT,
  input  R_TYPE,
  output JR
);

  and and_1 (JR, ~FUNCT[5], ~FUNCT[4], FUNCT[3], ~FUNCT[2], ~FUNCT[1], ~FUNCT[0], R_TYPE);  // AND_Gate
endmodule

module BIT_EXTENDER (
  input  [15:0] IN_16b,
  input  ExtOp,
  output [31:0] OUT_32b
);

  wire and_1_out;

  and and_1 (and_1_out, IN_16b[15], ExtOp);
  assign OUT_32b = {{16{and_1_out}}, IN_16b};  // Bit_Extender bit_extender_1
endmodule
